// Logisim project ex1.circ as structural Verilog
module main (
  input  X_AND,
  input  X_OR,
  input  Y_AND,
  input  Y_OR,
  input  X_NAND,
  input  X_NOT,
  input  Y_NAND,
  input  X_NOR,
  input  X_XOR,
  input  Y_NOR,
  input  Y_XOR,
  input  X_XNOR,
  input  Y_XNOR,
  input  X,
  input  Y,
  output Z_AND,
  output Z_OR,
  output Z_AND_VHDL,
  output Z_OR_VHDL,
  output Z_NOT,
  output Z_NAND,
  output Z_NOT_VHDL,
  output Z_NAND_VHDL,
  output Z_NOR,
  output Z_XOR,
  output Z_NOR_VHDL,
  output Z_XOR_VHDL,
  output Z_XNOR,
  output Z_XNOR_VHDL,
  output out_30,
  output out_31,
  output out_32,
  output out_33,
  output out_34,
  output out_35,
  output out_36,
  output out_37
);

  not not_1 (Z_NOT, X_NOT);
  and and_1 (Z_AND, X_AND, Y_AND);
  nor nor_1 (Z_NOR, X_NOR, Y_NOR);
  xnor xnor_1 (Z_XNOR, X_XNOR, Y_XNOR);
  VHDL_AND vhdl_and_1 (.X_AND(X_AND), .Y_AND(Y_AND), .Z_AND(Z_AND_VHDL));
  VHDL_NOR vhdl_nor_1 (.X_NOR(X_NOR), .Y_NOR(Y_NOR), .Z_NOR(Z_NOR_VHDL));
  VHDL_XNOR vhdl_xnor_1 (.X_XNOR(X_XNOR), .Y_XNOR(Y_XNOR), .Z_XNOR(Z_XNOR_VHDL));
  VHDL_PORTS vhdl_ports_1 (
    .X(X), .Y(Y), .AND_Z(out_30), .OR_Z(out_31), .NAND_Z(out_32), .NOR_Z(out_33), .XOR_Z(out_34),
    .XNOR_Z(out_35), .NOT_X_Z(out_36), .NOT_Y_Z(out_37));
  VHDL_NOT vhdl_not_1 (.X_NOT(X_NOT), .Z_NOT(Z_NOT_VHDL));
  or or_1 (Z_OR, X_OR, Y_OR);
  nand nand_1 (Z_NAND, X_NAND, Y_NAND);
  xor xor_1 (Z_XOR, X_XOR, Y_XOR);
  VHDL_OR vhdl_or_1 (.X_OR(X_OR), .Y_OR(Y_OR), .Z_OR(Z_OR_VHDL));
  VHDL_NAND vhdl_nand_1 (.X_NAND(X_NAND), .Y_NAND(Y_NAND), .Z_NAND(Z_NAND_VHDL));
  VHDL_XOR vhdl_xor_1 (.X_XOR(X_XOR), .Y_XOR(Y_XOR), .Z_XOR(Z_XOR_VHDL));

  // Notes on the sheet:
  //   XNOR
  //   AND
  //   NOT
  //   NOR
  //   NAND
  //   XOR
  //   OR
endmodule

// VHDL entity VHDL_AND, as the project stores it:
--------------------------------------------------------------------------------
-- Project :
-- File    :
-- Autor   :
-- Date    :
--
--------------------------------------------------------------------------------
-- Description :
--
--------------------------------------------------------------------------------

LIBRARY ieee;
USE ieee.std_logic_1164.all;

ENTITY VHDL_AND IS
  PORT (
  ------------------------------------------------------------------------------
  --Insert input ports below
    X_AND      : IN  std_logic; -- input bit example
    Y_AND      : IN  std_logic; -- input bit example
  ------------------------------------------------------------------------------
  --Insert output ports below
    Z_AND      : OUT std_logic  -- output bit example
    );
END VHDL_AND;

--------------------------------------------------------------------------------
--Complete your VHDL description below
--------------------------------------------------------------------------------

ARCHITECTURE TypeArchitecture OF VHDL_AND IS

BEGIN

	Z_AND <= X_AND AND Y_AND;

END TypeArchitecture;

// VHDL entity VHDL_NOT, as the project stores it:
--------------------------------------------------------------------------------
-- Project :
-- File    :
-- Autor   :
-- Date    :
--
--------------------------------------------------------------------------------
-- Description :
--
--------------------------------------------------------------------------------

LIBRARY ieee;
USE ieee.std_logic_1164.all;

ENTITY VHDL_NOT IS
  PORT (
  ------------------------------------------------------------------------------
  --Insert input ports below
    X_NOT      : IN  std_logic; -- input bit example
    
  ------------------------------------------------------------------------------
  --Insert output ports below
    Z_NOT      : OUT std_logic  -- output bit example
    );
END VHDL_NOT;

--------------------------------------------------------------------------------
--Complete your VHDL description below
--------------------------------------------------------------------------------

ARCHITECTURE TypeArchitecture OF VHDL_NOT IS

BEGIN

	Z_NOT <= NOT X_NOT;

END TypeArchitecture;

// VHDL entity VHDL_OR, as the project stores it:
--------------------------------------------------------------------------------
-- Project :
-- File    :
-- Autor   :
-- Date    :
--
--------------------------------------------------------------------------------
-- Description :
--
--------------------------------------------------------------------------------

LIBRARY ieee;
USE ieee.std_logic_1164.all;

ENTITY VHDL_OR IS
  PORT (
  ------------------------------------------------------------------------------
  --Insert input ports below
    X_OR      : IN  std_logic; -- input bit example
    Y_OR      : IN  std_logic; -- input bit example
  ------------------------------------------------------------------------------
  --Insert output ports below
    Z_OR      : OUT std_logic  -- output bit example
    );
END VHDL_OR;

--------------------------------------------------------------------------------
--Complete your VHDL description below
--------------------------------------------------------------------------------

ARCHITECTURE TypeArchitecture OF VHDL_OR IS

BEGIN

	Z_OR <= X_OR OR Y_OR;

END TypeArchitecture;

// VHDL entity VHDL_NAND, as the project stores it:
--------------------------------------------------------------------------------
-- Project :
-- File    :
-- Autor   :
-- Date    :
--
--------------------------------------------------------------------------------
-- Description :
--
--------------------------------------------------------------------------------

LIBRARY ieee;
USE ieee.std_logic_1164.all;

ENTITY VHDL_NAND IS
  PORT (
  ------------------------------------------------------------------------------
  --Insert input ports below
    X_NAND      : IN  std_logic; -- input bit example
    Y_NAND      : IN  std_logic; -- input bit example
  ------------------------------------------------------------------------------
  --Insert output ports below
    Z_NAND      : OUT std_logic  -- output bit example
    );
END VHDL_NAND;

--------------------------------------------------------------------------------
--Complete your VHDL description below
--------------------------------------------------------------------------------

ARCHITECTURE TypeArchitecture OF VHDL_NAND IS

BEGIN

	Z_NAND <= X_NAND NAND Y_NAND;

END TypeArchitecture;

// VHDL entity VHDL_NOR, as the project stores it:
--------------------------------------------------------------------------------
-- Project :
-- File    :
-- Autor   :
-- Date    :
--
--------------------------------------------------------------------------------
-- Description :
--
--------------------------------------------------------------------------------

LIBRARY ieee;
USE ieee.std_logic_1164.all;

ENTITY VHDL_NOR IS
  PORT (
  ------------------------------------------------------------------------------
  --Insert input ports below
    X_NOR      : IN  std_logic; -- input bit example
    Y_NOR      : IN  std_logic; -- input bit example
  ------------------------------------------------------------------------------
  --Insert output ports below
    Z_NOR      : OUT std_logic  -- output bit example
    );
END VHDL_NOR;

--------------------------------------------------------------------------------
--Complete your VHDL description below
--------------------------------------------------------------------------------

ARCHITECTURE TypeArchitecture OF VHDL_NOR IS

BEGIN

	Z_NOR <= X_NOR NOR Y_NOR;

END TypeArchitecture;

// VHDL entity VHDL_XOR, as the project stores it:
--------------------------------------------------------------------------------
-- Project :
-- File    :
-- Autor   :
-- Date    :
--
--------------------------------------------------------------------------------
-- Description :
--
--------------------------------------------------------------------------------

LIBRARY ieee;
USE ieee.std_logic_1164.all;

ENTITY VHDL_XOR IS
  PORT (
  ------------------------------------------------------------------------------
  --Insert input ports below
    X_XOR      : IN  std_logic; -- input bit example
    Y_XOR      : IN  std_logic; -- input bit example
  ------------------------------------------------------------------------------
  --Insert output ports below
    Z_XOR      : OUT std_logic  -- output bit example
    );
END VHDL_XOR;

--------------------------------------------------------------------------------
--Complete your VHDL description below
--------------------------------------------------------------------------------

ARCHITECTURE TypeArchitecture OF VHDL_XOR IS

BEGIN

	Z_XOR <= X_XOR XOR Y_XOR;

END TypeArchitecture;

// VHDL entity VHDL_XNOR, as the project stores it:
--------------------------------------------------------------------------------
-- Project :
-- File    :
-- Autor   :
-- Date    :
--
--------------------------------------------------------------------------------
-- Description :
--
--------------------------------------------------------------------------------

LIBRARY ieee;
USE ieee.std_logic_1164.all;

ENTITY VHDL_XNOR IS
  PORT (
  ------------------------------------------------------------------------------
  --Insert input ports below
    X_XNOR      : IN  std_logic; -- input bit example
    Y_XNOR      : IN  std_logic; -- input bit example
  ------------------------------------------------------------------------------
  --Insert output ports below
    Z_XNOR      : OUT std_logic  -- output bit example
    );
END VHDL_XNOR;

--------------------------------------------------------------------------------
--Complete your VHDL description below
--------------------------------------------------------------------------------

ARCHITECTURE TypeArchitecture OF VHDL_XNOR IS

BEGIN

	Z_XNOR <= X_XNOR XNOR Y_XNOR;

END TypeArchitecture;

// VHDL entity VHDL_PORTS, as the project stores it:
--------------------------------------------------------------------------------
-- Project :
-- File    :
-- Autor   :
-- Date    :
--
--------------------------------------------------------------------------------
-- Description :
--
--------------------------------------------------------------------------------

LIBRARY ieee;
USE ieee.std_logic_1164.all;

ENTITY VHDL_PORTS IS
  PORT (
  ------------------------------------------------------------------------------
  --Insert input ports below
    X     : IN  std_logic;                    -- input bit example
    Y     : IN  std_logic;                    -- input bit example
  ------------------------------------------------------------------------------
  --Insert output ports below
    AND_Z       : OUT std_logic;                  -- output bit example
    OR_Z        : OUT std_logic;                  -- output bit example
    NAND_Z      : OUT std_logic;                  -- output bit example
    NOR_Z       : OUT std_logic;                  -- output bit example
    XOR_Z       : OUT std_logic;                  -- output bit example
    XNOR_Z      : OUT std_logic;                  -- output bit example
    NOT_X_Z     : OUT std_logic;                  -- output bit example
    NOT_Y_Z     : OUT std_logic                   -- output bit example

    );
END VHDL_PORTS;

--------------------------------------------------------------------------------
--Complete your VHDL description below
--------------------------------------------------------------------------------

ARCHITECTURE TypeArchitecture OF VHDL_PORTS IS

BEGIN
	
	AND_Z   <= X AND Y;
	OR_Z    <= X OR Y;
	NAND_Z  <= X NAND Y;
	NOR_Z   <= X NOR Y;
	XOR_Z   <= X XOR Y;
	XNOR_Z  <= X XNOR Y;
	NOT_X_Z <= NOT X;
	NOT_Y_Z <= NOT Y;

END TypeArchitecture;
