// Logisim project tutorial4.circ as structural Verilog
module main (
  input  X,
  input  Y,
  output Z,
  output Z_VHDL
);

  wire And1_out, And2_out, not_1_out, not_2_out;

  not not_1 (not_1_out, X);
  not not_2 (not_2_out, Y);
  and And1 (And1_out, not_1_out, Y);
  and And2 (And2_out, X, not_2_out);
  or or1 (Z, And1_out, And2_out);
  VHDL_XOR vhdl_xor_1 (.X(X), .Y(Y), .Z(Z_VHDL));

  // Notes on the sheet:
  //   XOR
  //   logisim-evolution
endmodule

// VHDL entity VHDL_XOR, as the project stores it:
--------------------------------------------------------------------------------
-- Project :
-- File    :
-- Autor   :
-- Date    :
--
--------------------------------------------------------------------------------
-- Description :
--
--------------------------------------------------------------------------------

LIBRARY ieee;
USE ieee.std_logic_1164.all;

ENTITY VHDL_XOR IS
  PORT (
  ------------------------------------------------------------------------------
  --Insert input ports below
    X      : IN  std_logic; -- input bit example
    Y      : IN  std_logic; -- input bit example
  ------------------------------------------------------------------------------
  --Insert output ports below
    Z      : OUT std_logic  -- output bit example
    );
END VHDL_XOR;

--------------------------------------------------------------------------------
--Complete your VHDL description below
--------------------------------------------------------------------------------

ARCHITECTURE TypeArchitecture OF VHDL_XOR IS

BEGIN

	Z <= X XOR Y;

END TypeArchitecture;
