// Logisim project p2ex1.circ as structural Verilog
module main (
  input  x,
  input  y,
  output nn_and_out,
  output nor_out,
  output nn_or_out,
  output nand_out,
  output vhdl_nor_out,
  output vhdl_nand_out,
  output vhdl_nn_and_out,
  output vhdl_nn_or_out
);

  wire not_1_out, not_2_out;

  nor nor_1 (nor_out, x, y);
  nand nand_1 (nand_out, x, y);
  p2ex1 p2ex1_1 (
    .x(y), .y(x), .nor_out(vhdl_nor_out), .nand_out(vhdl_nand_out), .nn_and_out(vhdl_nn_and_out),
    .nn_or_out(vhdl_nn_or_out));
  not not_1 (not_1_out, x);
  not not_2 (not_2_out, y);
  and and_1 (nn_and_out, not_1_out, not_2_out);
  or or_1 (nn_or_out, not_1_out, not_2_out);
endmodule

// VHDL entity p2ex1, as the project stores it:
--------------------------------------------------------------------------------
-- Project :
-- File    :
-- Autor   :
-- Date    :
--
--------------------------------------------------------------------------------
-- Description :
--
--------------------------------------------------------------------------------

LIBRARY ieee;
USE ieee.std_logic_1164.all;

ENTITY p2ex1 IS
  PORT (
  ------------------------------------------------------------------------------
  --Insert input ports below
    x          : IN  std_logic; -- input bit example
    y          : IN  std_logic; -- input bit example
  ------------------------------------------------------------------------------
  --Insert output ports below
    nor_out    : OUT std_logic; -- output bit example
    nand_out   : OUT std_logic;  -- output bit example
    nn_and_out : OUT std_logic;  -- output bit example
    nn_or_out  : OUT std_logic  -- output bit example
    );
END p2ex1;

--------------------------------------------------------------------------------
--Complete your VHDL description below
--------------------------------------------------------------------------------

ARCHITECTURE TypeArchitecture OF p2ex1 IS

BEGIN
	nor_out <= x nor y;
     nand_out <= x nand y;
     nn_and_out <= (not x) and (not y);
     nn_or_out <= (not x) or (not y);
END TypeArchitecture;
