// Logisim project p2ex2.circ as structural Verilog
module main (
  input  A,
  input  B,
  input  C,
  input  D,
  output X,
  output Y,
  output Z,
  output X_VHDL,
  output Y_VHDL,
  output Z_VHDL
);

  wire AND_1_out, and_1_out_2, AND_2_out, AND_3_out, nor_1_out, not_1_out, not_2_out, not_3_out, not_4_out,
       not_5_out, not_6_out, OR_1_out;

  and and_1 (and_1_out_2, C, D);
  not not_1 (not_1_out, A);
  not not_2 (not_2_out, B);
  not not_3 (not_3_out, A);
  not not_4 (not_4_out, B);
  not not_5 (not_5_out, C);
  nor nor_1 (nor_1_out, A, B);
  or OR_1 (OR_1_out, not_1_out, not_2_out);
  and AND_1_dup2 (AND_1_out, not_3_out, not_4_out, not_5_out);
  and AND_2 (AND_2_out, A, not_4_out, not_5_out);
  and AND_3 (AND_3_out, not_3_out, not_4_out, D);
  p2ex2 p2ex2_1 (.A(A), .B(B), .C(C), .D(D), .X(X_VHDL), .Y(Y_VHDL), .Z(Z_VHDL));
  and and_2_dup2 (X, nor_1_out, and_1_out_2);
  not not_6 (not_6_out, OR_1_out);
  and and_3_dup2 (Y, not_6_out, B, C);
  or or_1_dup2 (Z, AND_1_out, AND_2_out, AND_3_out);
endmodule

// VHDL entity p2ex2, as the project stores it:
--------------------------------------------------------------------------------
-- Project :
-- File    :
-- Autor   :
-- Date    :
--
--------------------------------------------------------------------------------
-- Description :
--
--------------------------------------------------------------------------------

LIBRARY ieee;
USE ieee.std_logic_1164.all;

ENTITY p2ex2 IS
  PORT (
  ------------------------------------------------------------------------------
  --Insert input ports below
    A        : IN  std_logic; -- input bit example
    B        : IN  std_logic; -- input bit example
    C        : IN  std_logic; -- input bit example
    D        : IN  std_logic; -- input bit example
  ------------------------------------------------------------------------------
  --Insert output ports below
    X        : OUT std_logic; -- output bit example
    Y        : OUT std_logic; -- output bit example
    Z        : OUT std_logic  -- output bit example
    );
END p2ex2;

--------------------------------------------------------------------------------
--Complete your VHDL description below
--------------------------------------------------------------------------------

ARCHITECTURE TypeArchitecture OF p2ex2 IS
SIGNAL OR_1, AND_1, AND_2, AND_3: std_logic;
BEGIN
	OR_1 <= not A or not B;
	AND_1 <= not A and not B and not C;
	AND_2 <= A and not B and not C;
	AND_3 <= not A and not B and D;
	X <= (A nor B) and (C and D);
	Y <= not OR_1 and B and C;
	Z <= AND_1 or AND_2 or AND_3;
END TypeArchitecture;
