// Logisim project p3e1.circ as structural Verilog
module main (
  input  [3:0] KLMN
);

  wire [6:0] dec_7s_1_c_7s, dec_7s_muxes_1_abcdefg;

  _7_Segment_Display u_7_segment_display_1 (
    .g(dec_7s_muxes_1_abcdefg[0]), .f(dec_7s_muxes_1_abcdefg[1]), .a(dec_7s_muxes_1_abcdefg[6]),
    .b(dec_7s_muxes_1_abcdefg[5]), .e(dec_7s_muxes_1_abcdefg[2]), .d(dec_7s_muxes_1_abcdefg[3]),
    .c(dec_7s_muxes_1_abcdefg[4]));  // open: dp
  _7_Segment_Display u_7_segment_display_2 (
    .g(dec_7s_1_c_7s[0]), .f(dec_7s_1_c_7s[1]), .a(dec_7s_1_c_7s[6]), .b(dec_7s_1_c_7s[5]),
    .e(dec_7s_1_c_7s[2]), .d(dec_7s_1_c_7s[3]), .c(dec_7s_1_c_7s[4]));  // open: dp
  dec_7s_muxes dec_7s_muxes_1 (.KLMN(KLMN), .ABCDEFG(dec_7s_muxes_1_abcdefg));
  dec_7s dec_7s_1 (.cnt_i(KLMN), .c_7s(dec_7s_1_c_7s));
endmodule

module dec_7s_muxes (
  input  [3:0] KLMN,
  output [6:0] ABCDEFG
);

  Multiplexer #(.select(4)) multiplexer_1 (
    .in0(1'b1), .in1(1'b0), .in2(1'b1), .in3(1'b1), .in4(1'b0), .in5(1'b1), .in6(1'b1), .in7(1'b1),
    .in8(1'b1), .in9(1'b1), .in10(1'b1), .in11(1'b0), .in12(1'b1), .in13(1'b0), .in14(1'b1), .in15(1'b0),
    .out(ABCDEFG[6]), .sel(KLMN));
  Multiplexer #(.select(4)) multiplexer_2 (
    .in0(1'b1), .in1(1'b0), .in2(1'b1), .in3(1'b0), .in4(1'b0), .in5(1'b0), .in6(1'b1), .in7(1'b0),
    .in8(1'b1), .in9(1'b0), .in10(1'b1), .in11(1'b1), .in12(1'b1), .in13(1'b1), .in14(1'b0), .in15(1'b1),
    .out(ABCDEFG[2]), .sel(KLMN));
  Multiplexer #(.select(4)) multiplexer_3 (
    .in0(1'b1), .in1(1'b0), .in2(1'b0), .in3(1'b0), .in4(1'b1), .in5(1'b1), .in6(1'b1), .in7(1'b0),
    .in8(1'b1), .in9(1'b1), .in10(1'b1), .in11(1'b1), .in12(1'b1), .in13(1'b0), .in14(1'b0), .in15(1'b0),
    .out(ABCDEFG[1]), .sel(KLMN));
  Multiplexer #(.select(4)) multiplexer_4 (
    .in0(1'b1), .in1(1'b1), .in2(1'b1), .in3(1'b1), .in4(1'b1), .in5(1'b0), .in6(1'b0), .in7(1'b1),
    .in8(1'b1), .in9(1'b1), .in10(1'b1), .in11(1'b0), .in12(1'b0), .in13(1'b1), .in14(1'b1), .in15(1'b1),
    .out(ABCDEFG[5]), .sel(KLMN));
  Multiplexer #(.select(4)) multiplexer_5 (
    .in0(1'b1), .in1(1'b1), .in2(1'b0), .in3(1'b1), .in4(1'b1), .in5(1'b1), .in6(1'b1), .in7(1'b1),
    .in8(1'b1), .in9(1'b1), .in10(1'b1), .in11(1'b1), .in12(1'b0), .in13(1'b1), .in14(1'b1), .in15(1'b1),
    .out(ABCDEFG[4]), .sel(KLMN));
  Multiplexer #(.select(4)) multiplexer_6 (
    .in0(1'b0), .in1(1'b0), .in2(1'b1), .in3(1'b1), .in4(1'b1), .in5(1'b1), .in6(1'b1), .in7(1'b0),
    .in8(1'b1), .in9(1'b1), .in10(1'b1), .in11(1'b1), .in12(1'b0), .in13(1'b1), .in14(1'b0), .in15(1'b0),
    .out(ABCDEFG[0]), .sel(KLMN));
  Multiplexer #(.select(4)) multiplexer_7 (
    .in0(1'b1), .in1(1'b0), .in2(1'b1), .in3(1'b1), .in4(1'b0), .in5(1'b1), .in6(1'b1), .in7(1'b0),
    .in8(1'b1), .in9(1'b0), .in10(1'b0), .in11(1'b1), .in12(1'b1), .in13(1'b1), .in14(1'b0), .in15(1'b1),
    .out(ABCDEFG[3]), .sel(KLMN));

  // Other names for the same wires on the sheet: N = KLMN[0]; M = KLMN[1]; L = KLMN[2]; K = KLMN[3]; G = ABCDEFG[0];
  //   F = ABCDEFG[1]; E = ABCDEFG[2]; D = ABCDEFG[3]; C = ABCDEFG[4]; B = ABCDEFG[5]; A = ABCDEFG[6]
endmodule

// VHDL entity dec_7s, as the project stores it:
LIBRARY ieee;
USE ieee.std_logic_1164.all;

ENTITY dec_7s IS
  PORT (
  ------------------------------------------------------------------------------
  -- Entradas (4 bits)
    cnt_i : IN  std_logic_vector(3 downto 0);
  ------------------------------------------------------------------------------
  -- Saídas (7 bits)
    c_7s  : OUT std_logic_vector(6 downto 0)
    );
END dec_7s;

--------------------------------------------------------------------------------
-- Saídas: abcdefg --- Entradas: klmn --
--------------------------------------------------------------------------------

ARCHITECTURE decode OF dec_7s IS

BEGIN
	WITH cnt_i SELECT
		c_7s <= "1111110" WHEN "0000",
			   "0110000" WHEN "0001",
			   "1101101" WHEN "0010",
			   "1111001" WHEN "0011",
			   "0110011" WHEN "0100",
			   "1011011" WHEN "0101",
			   "1011111" WHEN "0110",
			   "1110000" WHEN "0111",
			   "1111111" WHEN "1000",
			   "1110011" WHEN "1001",
			   "1110111" WHEN "1010",
			   "0011111" WHEN "1011",
			   "1001110" WHEN "1100",
			   "0111101" WHEN "1101",
			   "1110000" WHEN "1110",
			   "0111100" WHEN "1111",
			   "0000000" WHEN others;
END decode;
