// Logisim project pratica4.circ as structural Verilog
module latch_sr_nand_circuito (
  input  SET,
  input  RESET,
  output Q,
  output QN,
  output out_5,
  output out_6
);

  nand nand_1 (Q, SET, QN);
  nand nand_2 (QN, Q, RESET);
  latch_sr_nand latch_sr_nand_1 (.S(SET), .R(RESET), .Q(out_5), .QN(out_6));
endmodule

module latch_sr_nor_circuito (
  input  SET,
  input  RESET,
  output QN,
  output Q,
  output out_5,
  output out_6
);

  nor nor_1 (QN, SET, Q);
  nor nor_2 (Q, QN, RESET);
  latch_sr_nor latch_sr_nor_1 (.S(SET), .R(RESET), .Q(out_5), .QN(out_6));
endmodule

module latch_d_circuito (
  input  D,
  input  ENABLE,
  output out_3,
  output out_4,
  output out_5,
  output out_6,
  output out_7,
  output out_8,
  output out_9,
  output out_10,
  output out_11,
  output out_12,
  output out_13,
  output out_14
);

  wire nand_1_out, nand_2_out, nand_3_out, nand_4_out, nor_1_out, nor_2_out, nor_3_out, nor_4_out, not_1_out,
       not_2_out;

  not not_1 (not_1_out, D);
  not not_2 (not_2_out, D);
  nand nand_1 (nand_1_out, D, ENABLE);
  nand nand_2 (nand_2_out, ENABLE, nand_1_out);
  nor nor_1 (nor_1_out, D, ENABLE);
  nor nor_2 (nor_2_out, ENABLE, not_1_out);
  nor nor_3 (nor_3_out, D, ENABLE);
  nor nor_4 (nor_4_out, ENABLE, nor_3_out);
  nand nand_3 (nand_3_out, D, ENABLE);
  nand nand_4 (nand_4_out, ENABLE, not_2_out);
  nand nand_5 (out_4, nand_1_out, out_7);
  nand nand_6 (out_7, out_4, nand_2_out);
  nor nor_5 (out_9, nor_1_out, out_12);
  nor nor_6 (out_12, out_9, nor_2_out);
  nor nor_7 (out_10, nor_3_out, out_13);
  nor nor_8 (out_13, out_10, nor_4_out);
  latch_d_nand latch_d_nand_1 (.enable(ENABLE), .din(D), .q(out_5), .qn(out_8));
  latch_d_nor latch_d_nor_1 (.enable(ENABLE), .din(D), .q(out_11), .qn(out_14));
  nand nand_7 (out_3, nand_3_out, out_6);
  nand nand_8 (out_6, out_3, nand_4_out);

  // Notes on the sheet:
  //   SET
  //   LATCH D NOR
  //   RESET
  //   SET
  //   RESET
  //   SET
  //   LATCH D NAND
  //   RESET
  //   LATCH D NAND otimizado
  //   SET
  //   RESET
  //   LATCH D NOR otimizado
endmodule

module flip_flop_d_mestre_escravo_circuito (
  input  D,
  input  CLK,
  output out_3,
  output out_4,
  output out_5,
  output out_6,
  output out_7,
  output out_8,
  output out_9,
  output out_10,
  output out_11,
  output out_12,
  output out_13,
  output out_14
);

  wire nand_1_out, nand_2_out, nand_3_out, nand_4_out, nand_5_out, nand_6_out, nand_7_out, nand_8_out,
       nand_9_out, nand_10_out, nand_11_out, nand_12_out, nor_1_out, nor_2_out, nor_3_out, nor_4_out,
       nor_5_out, nor_6_out, nor_7_out, nor_8_out, nor_9_out, nor_10_out, nor_11_out, nor_12_out, not_1_out,
       not_2_out, undriven;

  not not_1 (not_1_out, CLK);
  not not_2 (not_2_out, undriven);
  nor nor_1 (nor_1_out, D, undriven);
  nor nor_2 (nor_2_out, undriven, nor_1_out);
  nor nor_3 (nor_3_out, D, not_2_out);
  nor nor_4 (nor_4_out, not_2_out, nor_3_out);
  nand nand_1 (nand_1_out, D, undriven);
  nand nand_2 (nand_2_out, undriven, nand_1_out);
  nand nand_3 (nand_3_out, D, not_1_out);
  nand nand_4 (nand_4_out, not_1_out, nand_3_out);
  flip_flop_d_positivo_mestre_escravo flip_flop_d_positivo_mestre_escravo_1 (
    .d(D), .clk(undriven), .q(out_4), .qn(out_7));
  nand nand_5 (nand_5_out, nand_3_out, nand_6_out);
  nand nand_6 (nand_6_out, nand_5_out, nand_4_out);
  nor nor_5 (nor_5_out, nor_1_out, nor_6_out);
  nor nor_6 (nor_6_out, nor_5_out, nor_2_out);
  flip_flop_d_negativo_mestre_escravo flip_flop_d_negativo_mestre_escravo_1 (
    .d(D), .clk(undriven), .q(out_10), .qn(out_13));
  nor nor_7 (nor_7_out, nor_3_out, nor_8_out);
  nor nor_8 (nor_8_out, nor_7_out, nor_4_out);
  nand nand_7 (nand_7_out, nand_1_out, nand_8_out);
  nand nand_8 (nand_8_out, nand_7_out, nand_2_out);
  nand nand_9 (nand_9_out, nor_5_out, undriven);
  nand nand_10 (nand_10_out, undriven, nand_9_out);
  nor nor_9 (nor_9_out, nor_7_out, undriven);
  nor nor_10 (nor_10_out, undriven, nor_9_out);
  nor nor_11 (nor_11_out, nand_7_out, undriven);
  nor nor_12 (nor_12_out, undriven, nor_11_out);
  nand nand_11 (nand_11_out, nand_5_out, undriven);
  nand nand_12 (nand_12_out, undriven, nand_11_out);
  nor nor_13 (out_9, nor_9_out, out_12);
  nor nor_14 (out_12, out_9, nor_10_out);
  nand nand_13 (out_3, nand_11_out, out_6);
  nand nand_14 (out_6, out_3, nand_12_out);
  nand nand_15 (out_5, nand_9_out, out_8);
  nand nand_16 (out_8, out_5, nand_10_out);
  nor nor_15 (out_11, nor_11_out, out_14);
  nor nor_16 (out_14, out_11, nor_12_out);

  // Notes on the sheet:
  //   SET
  //   RESET
  //   SET
  //   RESET
  //   SET
  //   RESET
  //   SET
  //   RESET
  //   Flip-flop D mestre escravo com resposta ao flanco positivo do clock
  //   Flip-flop D mestre escravo com resposta ao flanco negativo do clock
  //   Flip-flop D mestre escravo com resposta ao flanco positivo do clock otimizado
  //   Flip-flop D mestre escravo com resposta ao flanco negativo do clock otimizado
  //   SET
  //   RESET
  //   SET
  //   RESET
  //   SET
  //   RESET
  //   SET
  //   RESET
endmodule

module flip_flop_d_positivo_circuito (
  input  PRE,
  input  CLK,
  input  CLR,
  input  D,
  output Q,
  output out_6,
  output not_Q,
  output out_8
);

  wire nand_1_out, nand_2_out, nand_3_out, nand_4_out;

  nand nand_1 (nand_1_out, nand_4_out, nand_2_out);
  nand nand_2 (nand_2_out, nand_1_out, CLK);
  nand nand_3 (nand_3_out, nand_2_out, CLK, nand_4_out);
  nand nand_4 (nand_4_out, nand_3_out, D);
  flip_flop_d_positivo flip_flop_d_positivo_1 (.d(D), .clk(CLK), .rst(PRE), .clr(CLR), .q(out_6), .qn(out_8));
  nand nand_5 (Q, PRE, nand_2_out, not_Q);
  nand nand_6 (not_Q, Q, nand_3_out, CLR);
endmodule

module flip_flop_jk_circuito (
  input  PRE,
  input  CLR,
  input  CLK,
  input  J,
  input  K,
  output Q,
  output out_7,
  output out_8,
  output not_Q,
  output out_10,
  output out_11
);

  wire and_1_out, and_2_out, not_1_out, or_1_out;

  not not_1 (not_1_out, K);
  and and_1 (and_1_out, J, not_Q);
  and and_2 (and_2_out, not_1_out, Q);
  or or_1 (or_1_out, and_1_out, and_2_out);
  flip_flop_d_positivo_circuito flip_flop_d_positivo_circuito_1 (
    .PRE(PRE), .CLK(CLK), .CLR(CLR), .D(or_1_out), .Q(Q), .not_Q(not_Q));  // open: out_6, out_8
  flip_flop_jk_descritiva flip_flop_jk_descritiva_1 (
    .j(J), .k(K), .clr(CLR), .rst(PRE), .clk(CLK), .q(out_8), .qn(out_11));
  flip_flop_jk_logica flip_flop_jk_logica_1 (.j(J), .k(K), .clr(CLR), .rst(PRE), .clk(CLK), .q(out_7), .qn(out_10));
endmodule

module flip_flop_t_circuito (
  input  PRE,
  input  CLR,
  input  CLK,
  input  T,
  output Q,
  output out_6,
  output out_7,
  output not_Q,
  output out_9,
  output out_10
);

  wire xor_1_out;

  xor xor_1 (xor_1_out, T, Q);
  flip_flop_d_positivo_circuito flip_flop_d_positivo_circuito_1 (
    .PRE(PRE), .CLK(CLK), .CLR(CLR), .D(xor_1_out), .Q(Q), .not_Q(not_Q));  // open: out_6, out_8
  flip_flop_t_descritiva flip_flop_t_descritiva_1 (.t(T), .clr(CLR), .rst(PRE), .clk(CLK), .q(out_6), .qn(out_9));
  flip_flop_t_logica flip_flop_t_logica_1 (.t(T), .clr(CLR), .rst(PRE), .clk(CLK), .q(out_7), .qn(out_10));
endmodule

// VHDL entity latch_sr_nand, as the project stores it:
LIBRARY ieee;
USE ieee.std_logic_1164.all;

ENTITY latch_sr_nand IS
  PORT (
  ------------------------------------------------------------------------------
  --Insert input ports below
    S, R  : IN  std_logic; -- SET, RESET
  ------------------------------------------------------------------------------
  --Insert output ports below
    Q, QN : OUT std_logic -- Q, Q invertido
    );
END latch_sr_nand;

--------------------------------------------------------------------------------
--Complete your VHDL description below
--------------------------------------------------------------------------------

ARCHITECTURE TypeArchitecture OF latch_sr_nand IS

SIGNAL qstate: std_logic;

BEGIN

	PROCESS(S, R)
	BEGIN
		IF S = '0' AND R = '1' THEN qstate <= '1';
		ELSIF S = '1' AND R = '0' THEN qstate <= '0';
		END IF;
	END PROCESS;
	Q <= qstate;
	QN <= NOT qstate;
END TypeArchitecture;

// VHDL entity latch_sr_nor, as the project stores it:
LIBRARY ieee;
USE ieee.std_logic_1164.all;

ENTITY latch_sr_nor IS
  PORT (
  ------------------------------------------------------------------------------
  --Insert input ports below
    S, R  : IN  std_logic; -- SET, RESET
  ------------------------------------------------------------------------------
  --Insert output ports below
    Q, QN : OUT std_logic -- Q, Q invertido
    );
END latch_sr_nor;

--------------------------------------------------------------------------------
--Complete your VHDL description below
--------------------------------------------------------------------------------

ARCHITECTURE TypeArchitecture OF latch_sr_nor IS

SIGNAL qstate: std_logic;

BEGIN
	PROCESS(S, R)
	BEGIN
		IF S = '1' AND R = '0' THEN qstate <= '1';
		ELSIF S = '0' AND R = '1' THEN qstate <= '0';
		END IF;
	END PROCESS;
	Q <= qstate;
	QN <= NOT qstate;
END TypeArchitecture;

// VHDL entity latch_d_nand, as the project stores it:
LIBRARY ieee;
USE ieee.std_logic_1164.all;

ENTITY latch_d_nand IS
  PORT (
  ------------------------------------------------------------------------------
  --Insert input ports below
    enable, din : IN  std_logic; -- in: enable and data
  ------------------------------------------------------------------------------
  --Insert output ports below
    q, qn       : OUT std_logic  -- out
    );
END latch_d_nand;

--------------------------------------------------------------------------------
--Complete your VHDL description below
--------------------------------------------------------------------------------

ARCHITECTURE TypeArchitecture OF latch_d_nand IS

BEGIN
	PROCESS(enable, din)
	BEGIN
		IF enable = '1' THEN
			q <= din;
			qn <= NOT din;
		END IF;
	END PROCESS;
END TypeArchitecture;

// VHDL entity flip_flop_d_positivo_mestre_escravo, as the project stores it:
LIBRARY ieee;
USE ieee.std_logic_1164.all;

ENTITY flip_flop_d_positivo_mestre_escravo IS
  PORT (
    d, clk : IN  std_logic; -- input, clock
    q, qn  : OUT  std_logic -- output
    );
END flip_flop_d_positivo_mestre_escravo;

--------------------------------------------------------------------------------
--Complete your VHDL description below
--------------------------------------------------------------------------------

ARCHITECTURE latches OF flip_flop_d_positivo_mestre_escravo IS

SIGNAL s1: std_logic;

BEGIN
	latch1:process(clk, d)
	BEGIN
		IF clk = '1' AND clk' EVENT THEN
			s1 <= d;
		END IF;
	END PROCESS;
	latch2: PROCESS(clk, s1)
	BEGIN
		IF clk = '0' AND clk' EVENT THEN
			q <= s1;
		END IF;
	END PROCESS latch2;
	qn <= NOT s1;
END latches;

// VHDL entity flip_flop_d_negativo_mestre_escravo, as the project stores it:
LIBRARY ieee;
USE ieee.std_logic_1164.all;

ENTITY flip_flop_d_negativo_mestre_escravo IS
  PORT (
    d, clk : IN  std_logic; -- input, clock
    q, qn  : OUT  std_logic -- output
    );
END flip_flop_d_negativo_mestre_escravo;

--------------------------------------------------------------------------------
--Complete your VHDL description below
--------------------------------------------------------------------------------

ARCHITECTURE latches OF flip_flop_d_negativo_mestre_escravo IS

SIGNAL s1: std_logic;

BEGIN
	latch1:process(clk, d)
	BEGIN
		IF clk = '0' AND clk' EVENT THEN
			s1 <= d;
		END IF;
	END PROCESS;
	latch2: PROCESS(clk, s1)
	BEGIN
		IF clk = '1' AND clk' EVENT THEN
			q <= s1;
		END IF;
	END PROCESS latch2;
	qn <= NOT s1;
END latches;

// VHDL entity latch_d_nor, as the project stores it:
LIBRARY ieee;
USE ieee.std_logic_1164.all;

ENTITY latch_d_nor IS
  PORT (
  ------------------------------------------------------------------------------
  --Insert input ports below
    enable, din : IN  std_logic; -- in: enable and data
  ------------------------------------------------------------------------------
  --Insert output ports below
    q, qn       : OUT std_logic  -- out
    );
END latch_d_nor;

--------------------------------------------------------------------------------
--Complete your VHDL description below
--------------------------------------------------------------------------------

ARCHITECTURE TypeArchitecture OF latch_d_nor IS

BEGIN
	PROCESS(enable, din)
	BEGIN
		IF enable = '0' THEN
			q <= din;
			qn <= NOT din;
		END IF;
	END PROCESS;
END TypeArchitecture;

// VHDL entity flip_flop_d_positivo, as the project stores it:
LIBRARY ieee;
USE ieee.std_logic_1164.all;

ENTITY flip_flop_d_positivo IS
  PORT (
    d, clk, rst, clr : IN  std_logic; -- input, clock
    q, qn            : OUT  std_logic -- output
    );
END flip_flop_d_positivo;

--------------------------------------------------------------------------------
--Complete your VHDL description below
--------------------------------------------------------------------------------

ARCHITECTURE flip_flop OF flip_flop_d_positivo IS
SIGNAL qstate: std_logic;
BEGIN
	PROCESS(clk, rst, clr)
	BEGIN
		IF clr = '0' THEN 
			qstate <= '0';
		ELSIF rst = '0' THEN
			qstate <= '1';
		ELSIF clk = '1' AND clk' EVENT THEN
			qstate <= d;
		END IF;
	END PROCESS;
	q <= qstate;
	qn <= NOT qstate;
END flip_flop;

// VHDL entity flip_flop_jk_descritiva, as the project stores it:
LIBRARY ieee;
USE ieee.std_logic_1164.all;

ENTITY flip_flop_jk_descritiva IS
  PORT (
    j, k, clr, rst, clk : IN  std_logic; -- input, clock
    q, qn               : OUT  std_logic -- output
    );
END flip_flop_jk_descritiva;

--------------------------------------------------------------------------------
--Complete your VHDL description below
--------------------------------------------------------------------------------

ARCHITECTURE flip_flop OF flip_flop_jk_descritiva IS
SIGNAL qstate: std_logic;
BEGIN
	PROCESS(clk, rst, clr)
	BEGIN
		IF clr = '0' THEN 
			qstate <= '0';
		ELSIF rst = '0' THEN
			qstate <= '1';
		ELSIF clk = '1' AND clk' EVENT THEN
			IF j = '1' AND k = '1' THEN
				qstate <= NOT qstate;
			ELSIF j = '1' AND k = '0' THEN
				qstate <= '1';
			ELSIF j = '0' AND k = '1' THEN
				qstate <= '0';
			END IF;
		END IF;
	END PROCESS;
	q <= qstate;
	qn <= NOT qstate;
END flip_flop;

// VHDL entity flip_flop_jk_logica, as the project stores it:
LIBRARY ieee;
USE ieee.std_logic_1164.all;

ENTITY flip_flop_jk_logica IS
  PORT (
    j, k, clr, rst, clk : IN  std_logic; -- input, clock
    q, qn               : OUT  std_logic -- output
    );
END flip_flop_jk_logica;

--------------------------------------------------------------------------------
--Complete your VHDL description below
--------------------------------------------------------------------------------

ARCHITECTURE flip_flop OF flip_flop_jk_logica IS
SIGNAL qstate: std_logic;
BEGIN
	PROCESS(clk, rst, clr)
	BEGIN
		IF clr = '0' THEN 
			qstate <= '0';
		ELSIF rst = '0' THEN
			qstate <= '1';
		ELSIF clk = '1' AND clk' EVENT THEN
			qstate <= (NOT k AND qstate) OR (NOT qstate AND j);
		END IF;
	END PROCESS;
	q <= qstate;
	qn <= NOT qstate;
END flip_flop;

// VHDL entity flip_flop_t_descritiva, as the project stores it:
LIBRARY ieee;
USE ieee.std_logic_1164.all;

ENTITY flip_flop_t_descritiva IS
  PORT (
    t, clr, rst, clk : IN  std_logic; -- input, clock
    q, qn               : OUT  std_logic -- output
    );
END flip_flop_t_descritiva;

--------------------------------------------------------------------------------
--Complete your VHDL description below
--------------------------------------------------------------------------------

ARCHITECTURE flip_flop OF flip_flop_t_descritiva IS
SIGNAL qstate: std_logic;
BEGIN
	PROCESS(clk, rst, clr)
	BEGIN
		IF clr = '0' THEN 
			qstate <= '0';
		ELSIF rst = '0' THEN
			qstate <= '1';
		ELSIF clk = '1' AND clk' EVENT THEN
			IF t = '1' THEN
				qstate <= NOT qstate;
			END IF;
		END IF;
	END PROCESS;
	q <= qstate;
	qn <= NOT qstate;
END flip_flop;

// VHDL entity flip_flop_t_logica, as the project stores it:
LIBRARY ieee;
USE ieee.std_logic_1164.all;

ENTITY flip_flop_t_logica IS
  PORT (
    t, clr, rst, clk : IN  std_logic; -- input, clock
    q, qn               : OUT  std_logic -- output
    );
END flip_flop_t_logica;

--------------------------------------------------------------------------------
--Complete your VHDL description below
--------------------------------------------------------------------------------

ARCHITECTURE flip_flop OF flip_flop_t_logica IS
SIGNAL qstate: std_logic;
BEGIN
	PROCESS(clk, rst, clr)
	BEGIN
		IF clr = '0' THEN 
			qstate <= '0';
		ELSIF rst = '0' THEN
			qstate <= '1';
		ELSIF clk = '1' AND clk' EVENT THEN
			qstate <= t XOR qstate;
		END IF;
	END PROCESS;
	q <= qstate;
	qn <= NOT qstate;
END flip_flop;

// VHDL entity ff_t_deb, as the project stores it:
LIBRARY ieee;
USE ieee.std_logic_1164.all;

ENTITY ff_t_deb IS
  PORT (
    t, clrn, prn, clk_button, clk_50m : IN  STD_LOGIC; -- input T, clear, preset, clock, clock 50M
    q, qn                             : OUT STD_LOGIC  -- output Q, not Q
    );
END ff_t_deb;

--------------------------------------------------------------------------------
-- VHDL description below
--------------------------------------------------------------------------------

ARCHITECTURE ff_t OF ff_t_deb IS

COMPONENT div_clk IS
	GENERIC(divisor : INTEGER := 5);
	PORT(
		clk_in  : IN STD_LOGIC; -- clock in
		clk_out : OUT STD_LOGIC -- clock divided
	);
END COMPONENT;

COMPONENT debounce IS
	GENERIC(counter_size : INTEGER := 1); -- generalizes counter capacity
	PORT(
		clk    : IN STD_LOGIC; -- clock in
		button : IN STD_LOGIC; -- input signal
		result : OUT STD_LOGIC -- debounced signal
	);
END COMPONENT;

SIGNAL qstate, clk_10ms, clk_deb, clk_50m_signal : STD_LOGIC; 
	
BEGIN
	clk_50m_signal <= clk_50m;
	
	clk_div_10ms : div_clk GENERIC MAP(divisor => 250000)
					       PORT MAP(clk_in => clk_50m_signal, clk_out => clk_10ms);
					   
	deb : debounce 	       PORT MAP(clk => clk_10ms, button => clk_button, result => clk_deb);
	
	PROCESS(clk_deb, prn, clrn) -- sensitivity list
	BEGIN
		IF clrn = '0' THEN
			qstate <= '0';
		ELSIF prn = '0' THEN
			qstate <= '1';
		ELSIF clk_deb = '1' AND clk_deb' EVENT THEN -- positive edge detector
			IF t = '1' THEN
				qstate <= NOT qstate;
			END IF;
		END IF;
	END PROCESS;
	
	q <= qstate;
	qn <= NOT qstate;
END ff_t;

// VHDL entity ff_jk_deb, as the project stores it:
LIBRARY ieee;
USE ieee.std_logic_1164.all;

ENTITY ff_jk_deb IS
  PORT (
    j, k, clrn, prn, clk, clk_50m : IN  STD_LOGIC; -- input T, clear, preset, clock, clock 50M
    q, qn               		  : OUT STD_LOGIC  -- output Q, not Q
    );
END ff_jk_deb;

--------------------------------------------------------------------------------
-- VHDL description below
--------------------------------------------------------------------------------

ARCHITECTURE ff_jk OF ff_jk_deb IS

COMPONENT div_clk IS
	GENERIC(divisor : INTEGER := 5);
	PORT(
		clk_in  : IN STD_LOGIC; -- clock in
		clk_out : OUT STD_LOGIC -- clock divided
	);
END COMPONENT;

COMPONENT debounce IS
	GENERIC(counter_size : INTEGER := 1); -- generalizes counter capacity
	PORT(
		clk    : IN STD_LOGIC; -- clock in
		button : IN STD_LOGIC; -- input signal
		result : OUT STD_LOGIC -- debounced signal
	);
END COMPONENT;

SIGNAL qstate, clk_10ms, clk_deb, clk_50m_signal : STD_LOGIC; 
	
BEGIN
	clk_50m_signal <= clk_50m;
	
	clk_div_10ms : div_clk GENERIC MAP(divisor => 250000)
					       PORT MAP(clk_in => clk_50m_signal, clk_out => clk_10ms);
					   
	deb : debounce 		   PORT MAP(clk => clk_10ms, button => clk, result => clk_deb);
	
	PROCESS(clk_deb, prn, clrn) -- sensitivity list
	BEGIN
		IF clrn = '0' THEN 
			qstate <= '0';
		ELSIF prn = '0' THEN
			qstate <= '1';
		ELSIF clk_deb = '1' AND clk_deb' EVENT THEN
			IF j = '1' AND k = '1' THEN
				qstate <= NOT qstate;
			ELSIF j = '1' AND k = '0' THEN
				qstate <= '1';
			ELSIF j = '0' AND k = '1' THEN
				qstate <= '0';
			END IF;
		END IF;
	END PROCESS;
	
	q <= qstate;
	qn <= NOT qstate;
END ff_jk;
