// Logisim project Lab_05_P1_info.circ as structural Verilog
module components (
);

  dff vhdl ();  // open: d, clk, prs, clr, q, qn
  cnt_up_down_mod10 vhdl10 ();  // open: clk, z, ud, q, co
  cnt_up_down_mod6 vhdl6 ();  // open: clk, z, ud, q
  debounce vhdl_deb ();  // open: clk, button, result
  div_clk vhdl_div ();  // open: clk_in, clk_out
endmodule

module P0 (
  input  in_1,
  input  in_2,
  input  in_3,
  input  in_4,
  output out_5,
  output out_6
);

  dff dff_1 (.d(in_1), .clk(in_2), .prs(in_3), .clr(in_4), .q(out_5), .qn(out_6));
endmodule

module P1 (
);

  wire CLK_out, FF0_qn, FF1_qn, FF2_qn, FF3_qn, not_1_out, Q0, Q1, Q2, Q3, Z_out;
  wire [3:0] cnt_up_mod16_1_q;

  Clock CLK (.out(CLK_out));
  Button #(.press("passive")) Z (.out(Z_out));
  D_Flip_Flop FF0 (.D(FF0_qn), .clk(CLK_out), .Q(Q0), .Qn(FF0_qn), .reset(not_1_out));  // open: preset
  not not_1 (not_1_out, Z_out);
  D_Flip_Flop FF1 (.D(FF1_qn), .clk(FF0_qn), .Q(Q1), .Qn(FF1_qn), .reset(not_1_out));  // open: preset
  D_Flip_Flop FF2 (.D(FF2_qn), .clk(FF1_qn), .Q(Q2), .Qn(FF2_qn), .reset(not_1_out));  // open: preset
  Hex_Digit_Display hex_digit_display_1 (.value(cnt_up_mod16_1_q));  // open: dp
  cnt_up_mod16 cnt_up_mod16_1 (.clk(CLK_out), .z(Z_out), .q(cnt_up_mod16_1_q));
  D_Flip_Flop FF3 (.D(FF3_qn), .clk(FF2_qn), .Q(Q3), .Qn(FF3_qn), .reset(not_1_out));  // open: preset
  Hex_Digit_Display hex_digit_display_2 (.value({Q3, Q2, Q1, Q0}));  // open: dp
endmodule

module P2 (
);

  wire and_1_out, CLK_out, FF0_qn, FF1_qn, FF2_qn, FF3_qn, not_1_out, or_1_out, Q0, Q1, Q2, Q3, Z_out;
  wire [3:0] cnt_up_mod10_1_q;

  Clock CLK (.out(CLK_out));
  Button #(.press("passive")) Z (.out(Z_out));
  D_Flip_Flop FF0 (.D(FF0_qn), .clk(CLK_out), .Q(Q0), .Qn(FF0_qn), .reset(or_1_out));  // open: preset
  or or_1 (or_1_out, not_1_out, and_1_out);
  not not_1 (not_1_out, Z_out);
  D_Flip_Flop FF1 (.D(FF1_qn), .clk(FF0_qn), .Q(Q1), .Qn(FF1_qn), .reset(or_1_out));  // open: preset
  and and_1 (and_1_out, Q1, Q3);
  D_Flip_Flop FF2 (.D(FF2_qn), .clk(FF1_qn), .Q(Q2), .Qn(FF2_qn), .reset(or_1_out));  // open: preset
  cnt_up_mod10 cnt_up_mod10_1 (.clk(CLK_out), .z(Z_out), .q(cnt_up_mod10_1_q));
  D_Flip_Flop FF3 (.D(FF3_qn), .clk(FF2_qn), .Q(Q3), .Qn(FF3_qn), .reset(or_1_out));  // open: preset
  Hex_Digit_Display hex_digit_display_1 (.value(cnt_up_mod10_1_q));  // open: dp
  Hex_Digit_Display hex_digit_display_2 (.value({Q3, Q2, Q1, Q0}));  // open: dp
endmodule

module P3 (
);

  wire and_1_out, and_2_out, CLK_out, d_ff_1_q, FF0_qn, FF1_qn, FF2_qn, FF3_qn, not_1_out, not_2_out,
       or_1_out, Q0, Q1, Q2, Q3, Z_out;
  wire [3:0] cnt_up_mod10_alarg_1_q;

  Clock CLK (.out(CLK_out));
  not not_1 (not_1_out, Z_out);
  Button #(.press("passive")) Z (.out(Z_out));
  D_Flip_Flop FF0 (.D(FF0_qn), .clk(CLK_out), .Q(Q0), .Qn(FF0_qn), .reset(or_1_out));  // open: preset
  or or_1 (or_1_out, not_1_out, and_1_out, d_ff_1_q);
  not not_2 (not_2_out, CLK_out);
  D_Flip_Flop FF1 (.D(FF1_qn), .clk(FF0_qn), .Q(Q1), .Qn(FF1_qn), .reset(or_1_out));  // open: preset
  and and_1 (and_1_out, Q1, Q3);
  D_Flip_Flop FF2 (.D(FF2_qn), .clk(FF1_qn), .Q(Q2), .Qn(FF2_qn), .reset(or_1_out));  // open: preset
  cnt_up_mod10_alarg cnt_up_mod10_alarg_1 (.clk(CLK_out), .z(Z_out), .q(cnt_up_mod10_alarg_1_q));
  D_Flip_Flop FF3 (.D(FF3_qn), .clk(FF2_qn), .Q(Q3), .Qn(FF3_qn), .reset(or_1_out));  // open: preset
  Hex_Digit_Display hex_digit_display_1 (.value(cnt_up_mod10_alarg_1_q));  // open: dp
  Hex_Digit_Display hex_digit_display_2 (.value({Q3, Q2, Q1, Q0}));  // open: dp
  and and_2 (and_2_out, ~Q0, Q1, ~Q2, Q3);  // AND_Gate
  D_Flip_Flop d_ff_1 (.Q(d_ff_1_q), .preset(and_2_out), .reset(not_2_out));  // open: D, clk, Qn
endmodule

module P4 (
);

  wire and_1_out, CLK_out, FF0_qn, FF1_qn, FF2_qn, not_1_out, or_1_out, Q0, Q1, Q2, Z_out;
  wire [3:0] cnt_up_mod6_1_q;

  Clock CLK (.out(CLK_out));
  Button #(.press("passive")) Z (.out(Z_out));
  D_Flip_Flop FF0 (.D(FF0_qn), .clk(CLK_out), .Q(Q0), .Qn(FF0_qn), .reset(or_1_out));  // open: preset
  or or_1 (or_1_out, not_1_out, and_1_out);
  not not_1 (not_1_out, Z_out);
  D_Flip_Flop FF1 (.D(FF1_qn), .clk(FF0_qn), .Q(Q1), .Qn(FF1_qn), .reset(or_1_out));  // open: preset
  and and_1 (and_1_out, Q1, Q2);
  D_Flip_Flop FF2 (.D(FF2_qn), .clk(FF1_qn), .Q(Q2), .Qn(FF2_qn), .reset(or_1_out));  // open: preset
  Hex_Digit_Display hex_digit_display_1 (.value(cnt_up_mod6_1_q));  // open: dp
  cnt_up_mod6 cnt_up_mod6_1 (.clk(CLK_out), .z(Z_out), .q(cnt_up_mod6_1_q));
  Hex_Digit_Display hex_digit_display_2 (.value({1'b0, Q2, Q1, Q0}));  // open: dp
endmodule

module P5 (
);

  wire and_1_out, and_2_out, CLK_out, d_ff_1_q, FF0_qn, FF1_qn, FF2_qn, not_1_out, not_2_out, or_1_out, Q0,
       Q1, Q2, Z_out;
  wire [3:0] cnt_up_mod6_alarg_1_q;

  Clock CLK (.out(CLK_out));
  Button #(.press("passive")) Z (.out(Z_out));
  D_Flip_Flop FF0 (.D(FF0_qn), .clk(CLK_out), .Q(Q0), .Qn(FF0_qn), .reset(or_1_out));  // open: preset
  not not_1 (not_1_out, CLK_out);
  or or_1 (or_1_out, not_2_out, and_1_out, d_ff_1_q);
  not not_2 (not_2_out, Z_out);
  D_Flip_Flop FF1 (.D(FF1_qn), .clk(FF0_qn), .Q(Q1), .Qn(FF1_qn), .reset(or_1_out));  // open: preset
  and and_1 (and_1_out, Q1, Q2);
  D_Flip_Flop FF2 (.D(FF2_qn), .clk(FF1_qn), .Q(Q2), .Qn(FF2_qn), .reset(or_1_out));  // open: preset
  Hex_Digit_Display hex_digit_display_1 (.value(cnt_up_mod6_alarg_1_q));  // open: dp
  cnt_up_mod6_alarg cnt_up_mod6_alarg_1 (.clk(CLK_out), .z(Z_out), .q(cnt_up_mod6_alarg_1_q));
  Hex_Digit_Display hex_digit_display_2 (.value({1'b0, Q2, Q1, Q0}));  // open: dp
  and and_2 (and_2_out, ~Q0, Q1, Q2);  // AND_Gate
  D_Flip_Flop d_ff_1 (.Q(d_ff_1_q), .preset(and_2_out), .reset(not_1_out));  // open: D, clk, Qn
endmodule

module P6 (
);

  wire CLK_out, FF0_qn, FF1_qn, FF2_qn, FF3_qn, not_1_out, Q0, Q1, Q2, Q3, Z_out;
  wire [3:0] cnt_down_mod16_1_q;

  Clock CLK (.out(CLK_out));
  Button #(.press("passive")) Z (.out(Z_out));
  D_Flip_Flop FF0 (.D(FF0_qn), .clk(CLK_out), .Q(Q0), .Qn(FF0_qn), .reset(not_1_out));  // open: preset
  not not_1 (not_1_out, Z_out);
  D_Flip_Flop FF1 (.D(FF1_qn), .clk(Q0), .Q(Q1), .Qn(FF1_qn), .reset(not_1_out));  // open: preset
  D_Flip_Flop FF2 (.D(FF2_qn), .clk(Q1), .Q(Q2), .Qn(FF2_qn), .reset(not_1_out));  // open: preset
  Hex_Digit_Display hex_digit_display_1 (.value(cnt_down_mod16_1_q));  // open: dp
  cnt_down_mod16 cnt_down_mod16_1 (.clk(CLK_out), .z(Z_out), .q(cnt_down_mod16_1_q));
  D_Flip_Flop FF3 (.D(FF3_qn), .clk(Q2), .Q(Q3), .Qn(FF3_qn), .reset(not_1_out));  // open: preset
  Hex_Digit_Display hex_digit_display_2 (.value({Q3, Q2, Q1, Q0}));  // open: dp
endmodule

module P7 (
);

  wire CLK_out, d_ff_1_q, F_out, FF0_qn, FF1_qn, FF2_qn, FF3_qn, not_1_out, or_1_out, Q0, Q1, Q2, Q3, RSTD,
       Z_out, ZR_out;
  wire [3:0] cnt_down_mod10_1_q;

  Clock CLK (.out(CLK_out));
  Button #(.press("passive")) Z (.out(Z_out));
  D_Flip_Flop FF0 (.D(FF0_qn), .clk(CLK_out), .Q(Q0), .Qn(FF0_qn), .preset(or_1_out), .reset(not_1_out));
  not not_1 (not_1_out, Z_out);
  D_Flip_Flop FF1 (.D(FF1_qn), .clk(Q0), .Q(Q1), .Qn(FF1_qn), .reset(or_1_out));  // open: preset
  or or_1 (or_1_out, not_1_out, RSTD);
  D_Flip_Flop FF2 (.D(FF2_qn), .clk(Q1), .Q(Q2), .Qn(FF2_qn), .reset(or_1_out));  // open: preset
  Hex_Digit_Display hex_digit_display_1 (.value(cnt_down_mod10_1_q));  // open: dp
  cnt_down_mod10 cnt_down_mod10_1 (.clk(CLK_out), .z(Z_out), .q(cnt_down_mod10_1_q));
  D_Flip_Flop FF3 (.D(FF3_qn), .clk(Q2), .Q(Q3), .Qn(FF3_qn), .preset(or_1_out), .reset(not_1_out));
  Hex_Digit_Display hex_digit_display_2 (.value({Q3, Q2, Q1, Q0}));  // open: dp
  and F (F_out, Q0, Q1, Q2, Q3);
  D_Flip_Flop d_ff_1 (.Q(d_ff_1_q), .preset(ZR_out), .reset(RSTD));  // open: D, clk, Qn
  nor ZR (ZR_out, Q0, Q1, Q2, Q3);
  and R (RSTD, F_out, d_ff_1_q);
endmodule

module P8 (
);

  wire and_1_out, and_3_out, button_1_out, clock_1_out, d_ff_1_qn, d_ff_2_qn, d_ff_3_qn, d_ff_4_qn, d_ff_5_q,
       nor_1_out, not_1_out, not_2_out, or_1_out, or_2_out, Q0, Q1, Q2, Q3, Q_ALARG, RSTD;
  wire [3:0] cnt_down_mod10_alarg_1_q;

  D_Flip_Flop d_ff_1 (.D(d_ff_1_qn), .clk(clock_1_out), .Q(Q0), .Qn(d_ff_1_qn), .preset(or_2_out), .reset(or_1_out));
  Clock clock_1 (.out(clock_1_out));
  or or_1 (or_1_out, not_1_out, Q_ALARG);
  not not_1 (not_1_out, button_1_out);
  Button #(.press("passive")) button_1 (.out(button_1_out));
  D_Flip_Flop d_ff_2 (.D(d_ff_2_qn), .clk(Q0), .Q(Q1), .Qn(d_ff_2_qn), .reset(or_2_out));  // open: preset
  not not_2 (not_2_out, clock_1_out);
  or or_2 (or_2_out, or_1_out, RSTD);
  D_Flip_Flop d_ff_3 (.D(d_ff_3_qn), .clk(Q1), .Q(Q2), .Qn(d_ff_3_qn), .reset(or_2_out));  // open: preset
  Hex_Digit_Display hex_digit_display_1 (.value(cnt_down_mod10_alarg_1_q));  // open: dp
  cnt_down_mod10_alarg cnt_down_mod10_alarg_1 (.clk(clock_1_out), .z(button_1_out), .q(cnt_down_mod10_alarg_1_q));
  D_Flip_Flop d_ff_4 (.D(d_ff_4_qn), .clk(Q2), .Q(Q3), .Qn(d_ff_4_qn), .preset(or_2_out), .reset(or_1_out));
  Hex_Digit_Display hex_digit_display_2 (.value({Q3, Q2, Q1, Q0}));  // open: dp
  and and_1 (and_1_out, Q0, Q1, Q2, Q3);
  nor nor_1 (nor_1_out, Q0, Q1, Q2, Q3);
  D_Flip_Flop d_ff_5 (.Q(d_ff_5_q), .preset(nor_1_out), .reset(RSTD));  // open: D, clk, Qn
  and and_2 (RSTD, and_1_out, d_ff_5_q);
  and and_3 (and_3_out, ~Q0, Q1, ~Q2, Q3);  // AND_Gate
  D_Flip_Flop d_ff_6 (.Q(Q_ALARG), .preset(and_3_out), .reset(not_2_out));  // open: D, clk, Qn
endmodule

module P9 (
);

  wire CLK_out, d_ff_1_q, F_out, FF0_qn, FF1_qn, FF2_qn, not_1_out, or_1_out, Q0, Q1, Q2, RSTD, Z_out, ZR_out;
  wire [3:0] cnt_down_mod6_1_q;

  Clock CLK (.out(CLK_out));
  Button #(.press("passive")) Z (.out(Z_out));
  D_Flip_Flop FF0 (.D(FF0_qn), .clk(CLK_out), .Q(Q0), .Qn(FF0_qn), .preset(or_1_out), .reset(not_1_out));
  not not_1 (not_1_out, Z_out);
  D_Flip_Flop FF1 (.D(FF1_qn), .clk(Q0), .Q(Q1), .Qn(FF1_qn), .reset(or_1_out));  // open: preset
  or or_1 (or_1_out, not_1_out, RSTD);
  D_Flip_Flop FF2 (.D(FF2_qn), .clk(Q1), .Q(Q2), .Qn(FF2_qn), .preset(or_1_out), .reset(not_1_out));
  Hex_Digit_Display hex_digit_display_1 (.value(cnt_down_mod6_1_q));  // open: dp
  cnt_down_mod6 cnt_down_mod6_1 (.clk(CLK_out), .z(Z_out), .q(cnt_down_mod6_1_q));
  Hex_Digit_Display hex_digit_display_2 (.value({1'b0, Q2, Q1, Q0}));  // open: dp
  D_Flip_Flop d_ff_1 (.Q(d_ff_1_q), .preset(ZR_out), .reset(RSTD));  // open: D, clk, Qn
  and F (F_out, Q0, Q1, Q2);
  nor ZR (ZR_out, Q0, Q1, Q2);
  and R (RSTD, F_out, d_ff_1_q);
endmodule

module P10 (
);

  wire and_1_out, CLK_out, d_ff_1_q, F_out, FF0_qn, FF1_qn, FF2_qn, not_1_out, not_2_out, or_1_out, or_2_out,
       Q0, Q1, Q2, Q_ALARG, RSTD, Z_out, ZR_out;
  wire [3:0] cnt_down_mod6_alarg_1_q;

  Clock CLK (.out(CLK_out));
  Button #(.press("passive")) Z (.out(Z_out));
  D_Flip_Flop FF0 (.D(FF0_qn), .clk(CLK_out), .Q(Q0), .Qn(FF0_qn), .preset(or_2_out), .reset(or_1_out));
  or or_1 (or_1_out, not_1_out, Q_ALARG);
  not not_1 (not_1_out, Z_out);
  not not_2 (not_2_out, CLK_out);
  D_Flip_Flop FF1 (.D(FF1_qn), .clk(Q0), .Q(Q1), .Qn(FF1_qn), .reset(or_2_out));  // open: preset
  or or_2 (or_2_out, or_1_out, RSTD);
  D_Flip_Flop FF2 (.D(FF2_qn), .clk(Q1), .Q(Q2), .Qn(FF2_qn), .preset(or_2_out), .reset(or_1_out));
  Hex_Digit_Display hex_digit_display_1 (.value(cnt_down_mod6_alarg_1_q));  // open: dp
  cnt_down_mod6_alarg cnt_down_mod6_alarg_1 (.clk(CLK_out), .z(Z_out), .q(cnt_down_mod6_alarg_1_q));
  Hex_Digit_Display hex_digit_display_2 (.value({1'b0, Q2, Q1, Q0}));  // open: dp
  D_Flip_Flop d_ff_1 (.Q(d_ff_1_q), .preset(ZR_out), .reset(RSTD));  // open: D, clk, Qn
  and F (F_out, Q0, Q1, Q2);
  nor ZR (ZR_out, Q0, Q1, Q2);
  and R (RSTD, F_out, d_ff_1_q);
  and and_1 (and_1_out, ~Q0, Q1, Q2);  // AND_Gate
  D_Flip_Flop d_ff_2 (.Q(Q_ALARG), .preset(and_1_out), .reset(not_2_out));  // open: D, clk, Qn
endmodule

module P11 (
  input  UD
);

  wire ALARG_out, CLK, CLKN, F_out, multiplexer_1_out, multiplexer_2_out, multiplexer_3_out,
       multiplexer_4_out, Q0, Q0N, Q1, Q1N, Q2, Q2N, Q3, Q3N, Q_ALARG, Q_DOWN, RST1, RST2, RST3, RST_DOWN,
       RST_UP, Z, ZN, ZR_out;
  wire [3:0] cnt_up_down_mod10_1_q;

  D_Flip_Flop FF_D0 (.D(Q0N), .clk(CLK), .Q(Q0), .Qn(Q0N), .preset(RST2), .reset(RST1));
  not not_1 (CLKN, CLK);
  Clock u_CLK (.out(CLK));
  Button #(.press("passive")) u_Z (.out(Z));
  or or_1 (RST1, ZN, RST_UP, Q_ALARG);
  not not_2 (ZN, Z);
  Multiplexer multiplexer_1 (.in0(Q0N), .in1(Q0), .out(multiplexer_1_out), .sel(UD));
  and and_1 (RST_UP, Q3, Q1, ~UD);  // AND_Gate
  D_Flip_Flop FF_D1 (.D(Q1N), .clk(multiplexer_1_out), .Q(Q1), .Qn(Q1N), .reset(RST3));  // open: preset
  or or_2 (RST2, ZN, multiplexer_2_out, RST_DOWN);
  Multiplexer multiplexer_2 (.in1(Q_ALARG), .out(multiplexer_2_out), .sel(UD));  // open: in0
  and F (F_out, Q0, Q1, Q2, Q3);
  nor ZR (ZR_out, Q0, Q1, Q2, Q3);
  D_Flip_Flop FF_DOWN (.Q(Q_DOWN), .preset(ZR_out), .reset(RST_DOWN));  // open: D, clk, Qn
  cnt_up_down_mod10 cnt_up_down_mod10_1 (.clk(CLK), .z(Z), .ud(UD), .q(cnt_up_down_mod10_1_q));  // open: co
  Hex_Digit_Display hex_digit_display_1 (.value(cnt_up_down_mod10_1_q));  // open: dp
  Hex_Digit_Display hex_digit_display_2 (.value({Q3, Q2, Q1, Q0}));  // open: dp
  and R (RST_DOWN, Q_DOWN, F_out, UD);
  Multiplexer multiplexer_3 (.in0(Q1N), .in1(Q1), .out(multiplexer_3_out), .sel(UD));
  or or_3 (RST3, RST1, Q_ALARG, RST2);
  D_Flip_Flop FF_D2 (.D(Q2N), .clk(multiplexer_3_out), .Q(Q2), .Qn(Q2N), .reset(RST3));  // open: preset
  and ALARG (ALARG_out, ~Q0, Q1, ~Q2, Q3);  // AND_Gate
  D_Flip_Flop FF_ALARG (.Q(Q_ALARG), .preset(ALARG_out), .reset(CLKN));  // open: D, clk, Qn
  Multiplexer multiplexer_4 (.in0(Q2N), .in1(Q2), .out(multiplexer_4_out), .sel(UD));
  D_Flip_Flop FF_D3 (.D(Q3N), .clk(multiplexer_4_out), .Q(Q3), .Qn(Q3N), .preset(RST2), .reset(RST1));

  // Notes on the sheet:
  //   unívoco
  //   alargador
endmodule

module P12 (
  input  UD
);

  wire ALARG_out, CLK, CLKN, F_out, multiplexer_1_out, multiplexer_2_out, Q0, Q0N, Q1, Q1N, Q2, Q2N, Q_ALARG,
       Q_DOWN, RST1, RST2, RST_DOWN, RST_UP, Z, ZN, ZR_out;
  wire [3:0] cnt_up_down_mod6_1_q;

  D_Flip_Flop FF_D0 (.D(Q0N), .clk(CLK), .Q(Q0), .Qn(Q0N), .preset(RST_DOWN), .reset(RST1));
  not not_1 (CLKN, CLK);
  Clock u_CLK (.out(CLK));
  Button #(.press("passive")) u_Z (.out(Z));
  or or_1 (RST1, ZN, RST_UP, Q_ALARG);
  not not_2 (ZN, Z);
  Multiplexer multiplexer_1 (.in0(Q0N), .in1(Q0), .out(multiplexer_1_out), .sel(UD));
  and and_1 (RST_UP, Q2, Q1, ~UD);  // AND_Gate
  D_Flip_Flop FF_D1 (.D(Q1N), .clk(multiplexer_1_out), .Q(Q1), .Qn(Q1N), .reset(RST2));  // open: preset
  or or_2 (RST2, RST1, RST_DOWN);
  and F (F_out, Q0, Q1, Q2);
  nor ZR (ZR_out, Q0, Q1, Q2);
  D_Flip_Flop FF_DOWN (.Q(Q_DOWN), .preset(ZR_out), .reset(RST_DOWN));  // open: D, clk, Qn
  cnt_up_down_mod6 cnt_up_down_mod6_1 (.clk(CLK), .z(Z), .ud(UD), .q(cnt_up_down_mod6_1_q));
  Hex_Digit_Display hex_digit_display_1 (.value(cnt_up_down_mod6_1_q));  // open: dp
  Hex_Digit_Display hex_digit_display_2 (.value({1'b0, Q2, Q1, Q0}));  // open: dp
  and R (RST_DOWN, Q_DOWN, F_out, UD);
  Multiplexer multiplexer_2 (.in0(Q1N), .in1(Q1), .out(multiplexer_2_out), .sel(UD));
  D_Flip_Flop FF_D2 (.D(Q2N), .clk(multiplexer_2_out), .Q(Q2), .Qn(Q2N), .preset(RST_DOWN), .reset(RST1));
  and ALARG (ALARG_out, ~Q0, Q1, Q2);  // AND_Gate
  D_Flip_Flop FF_ALARG (.Q(Q_ALARG), .preset(ALARG_out), .reset(CLKN));  // open: D, clk, Qn

  // Notes on the sheet:
  //   unívoco
  //   alargador
endmodule

module P13 (
  input  UD
);

  wire and_1_out, CLK_out, cnt_up_down_mod10_1_co, FF_SST_q, FF_SST_qn, not_1_out, SST_out, Z_out;
  wire [3:0] cnt_up_down_mod6_1_q, cnt_up_down_mod10_1_q, cnt_up_down_mod60_1_qd, cnt_up_down_mod60_1_qu;

  Button #(.press("passive")) SST (.out(SST_out));
  Clock CLK (.out(CLK_out));
  Button #(.press("passive")) Z (.out(Z_out));
  D_Flip_Flop FF_SST (.D(FF_SST_qn), .clk(SST_out), .Q(FF_SST_q), .Qn(FF_SST_qn), .reset(not_1_out));  // open: preset
  not not_1 (not_1_out, Z_out);
  and and_1 (and_1_out, FF_SST_q, CLK_out);
  cnt_up_down_mod10 cnt_up_down_mod10_1 (
    .clk(and_1_out), .z(Z_out), .ud(UD), .q(cnt_up_down_mod10_1_q), .co(cnt_up_down_mod10_1_co));
  cnt_up_down_mod6 cnt_up_down_mod6_1 (.clk(cnt_up_down_mod10_1_co), .z(Z_out), .ud(UD), .q(cnt_up_down_mod6_1_q));
  cnt_up_down_mod60 cnt_up_down_mod60_1 (
    .clk(CLK_out), .z(Z_out), .ud(UD), .sst(SST_out), .qu(cnt_up_down_mod60_1_qu), .qd(cnt_up_down_mod60_1_qd));
  Hex_Digit_Display hex_digit_display_1 (.value(cnt_up_down_mod6_1_q));  // open: dp
  Hex_Digit_Display hex_digit_display_2 (.value(cnt_up_down_mod10_1_q));  // open: dp
  Hex_Digit_Display hex_digit_display_3 (.value(cnt_up_down_mod60_1_qd));  // open: dp
  Hex_Digit_Display hex_digit_display_4 (.value(cnt_up_down_mod60_1_qu));  // open: dp
endmodule

// VHDL entity dff, as the project stores it:
--------------------------------------------------------------------------------
-- UTFPR - Universidade Tecnológica Federal do Paraná - Curitiba - PR
-- Projeto  : Prática 5 - Cronômetro
-- Circuito : Implementação de um FF tipo D
-- Arquivo  : dff_vhdl.vhd
-- Autor    : prof. Gortan
-- Data     : Maio 2022
--------------------------------------------------------------------------------
-- Descrição :
-- Implementa um flip-flop tipo D para ser usado como componente em outros circ.
-- obs.: O Logisim-evolution 3.7.2 irá armazenar esse componente
--       em uma biblioteca do Modelsim contida em:
-- 
--       C:\users\<nome_usuário>\AppData\Local\Temp\logisim\sim\comp\work 
--     
--       O Logisim-evolution criará um componente nesse local com o nome
--       da entity seguido de underline, seguido do nome do rótulo ou label
--       atribuido ao componente no circuito.
--
--       Neste projeto:
--       	a entity para o flip-flop tipo D será: dff
--          o rótulo (label) usado para o componente no circuito será: vhdl
--       Consequentemente o logisim criará um componente chamado dff_vhdl
--
--       É possível verificar no diretório:
--       C:\users\<nome_usuário>\AppData\Local\Temp\logisim\sim\src
--       que o Logisim-evolution realmente modificou o nome
--       do arquivo para dff_vhdl.vhdl e da entity para dff_vhdl
--
--       Esse será portanto o nome do componente referenciado em todos os
--       demais circuitos que fizerem uso desse componente.
--
--       Ao exportar este arquivo para o Quartus lembrar de renomear a entity
--       para dff_vhdl para que possa ser referenciada pelos outros circuitos.
--
--       Atenção: O Logisim-evolution não apaga o conteúdo da biblioteca "work"
--                citada acima. 
--				  Isso pode tanto ajudar como atrapalhar novos projetos
--                (dependendo do conteúdo de projetos anteriores estar
--                ou não de acordo com as necessidades do projeto atual)
--                Por esse motivo é sempre aconselhável apagar essa bibioteca
--                "work" antes de iniciar um novo projeto e também apagar a
--                pasta    C:\users\<nome_usuário>\AppData\Local\Temp\work
--                usada pelo Logisim-evolution como uma especie de cache.
--       O professor apagará sempre essas duas pastas antes de iniciar a 
--       validação de trabalhos submetidos por alunos. Não deixe de fazer isso
--       também antes de realizar uma última verificação para postar seus trabalhos
--------------------------------------------------------------------------------

--============================= Módulo comps: ==================================
library ieee;
  use ieee.std_logic_1164.all;

--==================== Componente: =============================================
library ieee;
  use ieee.std_logic_1164.all;

entity dff is								-- nome da entity será alterado
  port(
    d, clk, prs, clr	: in  std_logic;	-- entradas: dado, clk, preset e clear
    q, qn				: out std_logic	-- saídas:   q e q invertido
 );
end dff;

architecture ff_d of dff is

	signal qstate: std_logic;

begin
	process(clk, clr, prs)
	begin
		if clr = '1' then qstate <= '0';	 -- clr tem prioridade
		elsif prs = '1' then qstate <= '1'; -- sobre prs
		elsif clk = '1' and clk' event then qstate <= d;
		end if;
	end process;
	q <= qstate;
	qn <= not qstate;
end ff_d;

// VHDL entity cnt_up_mod16, as the project stores it:
--------------------------------------------------------------------------------
-- UTFPR - Universidade Tecnológica Federal do Paraná - Curitiba - PR
-- Projeto  : Prática 5 - Cronômetro
-- Circuito : Contador assíncrono ascendente módulo 16
-- Arquivo  : cnt_up_mod16.vhd
-- Autor    : prof. Gortan
-- Data     : Maio 2022
--------------------------------------------------------------------------------
-- Descrição :
-- Implementa um contador assíncrono ascendente módulo 16
-- Utiliza ffs tipo D com resposta a flanco positivo do clock e clear e preset
-- assíncronos ativos em alto (componente dff referenciado como dff_vhdl)
--------------------------------------------------------------------------------

--============================= Nível Superior: =========================================
library ieee;
  use ieee.std_logic_1164.all;

entity cnt_up_mod16 is
  port(
    clk, z  : in  std_logic;					-- entradas clk, rst
    q       : out std_logic_vector(3 downto 0)	-- saída q3 até q0
 );
end cnt_up_mod16;

architecture cnt_up_mod16_arch of cnt_up_mod16 is
	signal zn: std_logic;
	signal qn: std_logic_vector(3 downto 0);	-- liga qn com d
	component dff_vhdl is					-- dff referenciado como dff_vhdl
		port
		(
			d, clk, prs, clr	: in  std_logic;	-- entradas: dado, clk, preset e clear
			q, qn			: out std_logic 	-- saídas:   q e q invertido
		);
	end component;
begin
	zn <= not z;
	ff_d0: dff_vhdl port map(d => qn(0), prs => '0', clr => zn, clk => clk,   q => q(0), qn => qn(0));
	ff_d1: dff_vhdl port map(d => qn(1), prs => '0', clr => zn, clk => qn(0), q => q(1), qn => qn(1));
	ff_d2: dff_vhdl port map(d => qn(2), prs => '0', clr => zn, clk => qn(1), q => q(2), qn => qn(2));
	ff_d3: dff_vhdl port map(d => qn(3), prs => '0', clr => zn, clk => qn(2), q => q(3), qn => qn(3));

end cnt_up_mod16_arch;

// VHDL entity cnt_up_mod10, as the project stores it:
library ieee;
  use ieee.std_logic_1164.all;

entity cnt_up_mod10 is
  port(
    clk, z  : in  std_logic;					-- entradas clk, rst
    q       : out std_logic_vector(3 downto 0)	-- saída q3 até q0
 );
end cnt_up_mod10;

architecture cnt_up_mod10_arch of cnt_up_mod10 is
	signal zn, clr_signal: std_logic;
	signal qn, q_signal: std_logic_vector(3 downto 0);	-- liga qn com d
	component dff_vhdl is					-- dff referenciado como dff_vhdl
		port
		(
			d, clk, prs, clr	: in  std_logic;	-- entradas: dado, clk, preset e clear
			q, qn			: out std_logic 	-- saídas:   q e q invertido
		);
	end component;
begin
	zn <= not z;
	ff_d0: dff_vhdl port map(d => qn(0), prs => '0', clr => clr_signal, clk => clk,   q => q_signal(0), qn => qn(0));
	ff_d1: dff_vhdl port map(d => qn(1), prs => '0', clr => clr_signal, clk => qn(0), q => q_signal(1), qn => qn(1));
	ff_d2: dff_vhdl port map(d => qn(2), prs => '0', clr => clr_signal, clk => qn(1), q => q_signal(2), qn => qn(2));
	ff_d3: dff_vhdl port map(d => qn(3), prs => '0', clr => clr_signal, clk => qn(2), q => q_signal(3), qn => qn(3));
	clr_signal <= zn or (q_signal(1) and q_signal(3));
	q <= q_signal;
end cnt_up_mod10_arch;

// VHDL entity cnt_up_mod6, as the project stores it:
library ieee;
  use ieee.std_logic_1164.all;

entity cnt_up_mod6 is
  port(
    clk, z  : in  std_logic;					-- entradas clk, rst
    q       : out std_logic_vector(3 downto 0)	-- saída q3 até q0
 );
end cnt_up_mod6;

architecture cnt_up_mod6_arch of cnt_up_mod6 is
	signal zn, clr_signal: std_logic;
	signal qn, q_signal: std_logic_vector(3 downto 0);	-- liga qn com d
	component dff_vhdl is					-- dff referenciado como dff_vhdl
		port
		(
			d, clk, prs, clr	: in  std_logic;	-- entradas: dado, clk, preset e clear
			q, qn			: out std_logic 	-- saídas:   q e q invertido
		);
	end component;
begin
	zn <= not z;
	ff_d0: dff_vhdl port map(d => qn(0), prs => '0', clr => clr_signal, clk => clk,   q => q_signal(0), qn => qn(0));
	ff_d1: dff_vhdl port map(d => qn(1), prs => '0', clr => clr_signal, clk => qn(0), q => q_signal(1), qn => qn(1));
	ff_d2: dff_vhdl port map(d => qn(2), prs => '0', clr => clr_signal, clk => qn(1), q => q_signal(2), qn => qn(2));
	clr_signal <= zn or (q_signal(1) and q_signal(2));
	q_signal(3) <= '0';
	q <= q_signal;
end cnt_up_mod6_arch;

// VHDL entity cnt_down_mod16, as the project stores it:
library ieee;
use ieee.std_logic_1164.all;

entity cnt_down_mod16 is
    port(
        clk, z : in  std_logic;
        q      : out std_logic_vector(3 downto 0)
    );
end cnt_down_mod16;

architecture cnt_down_mod16_arch of cnt_down_mod16 is
    signal zn: std_logic;
    signal qn: std_logic_vector(3 downto 0);
    signal q_signal: std_logic_vector(3 downto 0);
    component dff_vhdl is
        port (
            d, clk, prs, clr : in  std_logic;
            q, qn            : out std_logic
        );
    end component;
begin
   	zn <= not z;

    	ff_d0: dff_vhdl port map(d => qn(0), prs => '0', clr => zn, clk => clk,  q => q_signal(0), qn => qn(0));
	ff_d1: dff_vhdl port map(d => qn(1), prs => '0', clr => zn, clk => q_signal(0), q => q_signal(1), qn => qn(1));
	ff_d2: dff_vhdl port map(d => qn(2), prs => '0', clr => zn, clk => q_signal(1), q => q_signal(2), qn => qn(2));
	ff_d3: dff_vhdl port map(d => qn(3), prs => '0', clr => zn, clk => q_signal(2), q => q_signal(3), qn => qn(3));
	q <= q_signal;
end cnt_down_mod16_arch;

// VHDL entity cnt_down_mod10, as the project stores it:
library ieee;
use ieee.std_logic_1164.all;

entity cnt_down_mod10 is
    port(
        clk, z : in  std_logic;
        q      : out std_logic_vector(3 downto 0)
    );
end cnt_down_mod10;

architecture cnt_down_mod10_arch of cnt_down_mod10 is
    signal zn, clrn, rstd, q_rstd, prs_rstd, qn_rstd, d_rstd, clk_rstd: std_logic;
    signal qn, q_signal: std_logic_vector(3 downto 0);
    
    component dff_vhdl is
        port (
            d, clk, prs, clr : in  std_logic;
            q, qn            : out std_logic
        );
    end component;
    
begin
    	ff_d0: dff_vhdl port map(d => qn(0), prs => clrn, clr => zn, clk => clk,  q => q_signal(0), qn => qn(0));
	ff_d1: dff_vhdl port map(d => qn(1), prs => '0', clr => clrn, clk => q_signal(0), q => q_signal(1), qn => qn(1));
	ff_d2: dff_vhdl port map(d => qn(2), prs => '0', clr => clrn, clk => q_signal(1), q => q_signal(2), qn => qn(2));
	ff_d3: dff_vhdl port map(d => qn(3), prs => clrn, clr => zn, clk => q_signal(2), q => q_signal(3), qn => qn(3));
	ff_rstd: dff_vhdl port map(d => d_rstd, prs => prs_rstd, clr => rstd, clk => clk_rstd, q => q_rstd, qn => qn_rstd);
	rstd <= q_rstd and (q_signal(0) and q_signal(1) and q_signal(2) and q_signal(3));
	prs_rstd <= not (q_signal(0) or q_signal(1) or q_signal(2) or q_signal(3));
   	zn <= not z;
	clrn <= zn or rstd;
	q <= q_signal;
end cnt_down_mod10_arch;

// VHDL entity cnt_down_mod6, as the project stores it:
library ieee;
use ieee.std_logic_1164.all;

entity cnt_down_mod6 is
    port(
        clk, z : in  std_logic;
        q      : out std_logic_vector(3 downto 0)
    );
end cnt_down_mod6;

architecture cnt_down_mod6_arch of cnt_down_mod6 is
    signal zn, clrn, rstd, q_rstd, prs_rstd, qn_rstd: std_logic;
    signal qn, q_signal: std_logic_vector(3 downto 0);
    
    component dff_vhdl is
        port (
            d, clk, prs, clr : in  std_logic;
            q, qn            : out std_logic
        );
    end component;
    
begin
    	ff_d0: dff_vhdl port map(d => qn(0), prs => clrn, clr => zn, clk => clk,  q => q_signal(0), qn => qn(0));
	ff_d1: dff_vhdl port map(d => qn(1), prs => '0', clr => clrn, clk => q_signal(0), q => q_signal(1), qn => qn(1));
	ff_d2: dff_vhdl port map(d => qn(2), prs => clrn, clr => zn, clk => q_signal(1), q => q_signal(2), qn => qn(2));
	ff_rstd: dff_vhdl port map(d => '0', prs => prs_rstd, clr => rstd, clk => '0', q => q_rstd, qn => qn_rstd);
	rstd <= q_rstd and (q_signal(0) and q_signal(1) and q_signal(2));
	prs_rstd <= not (q_signal(0) or q_signal(1) or q_signal(2));
   	zn <= not z;
	clrn <= zn or rstd;
	q_signal(3) <= '0';
	q <= q_signal;
end cnt_down_mod6_arch;

// VHDL entity cnt_up_mod10_alarg, as the project stores it:
library ieee;
  use ieee.std_logic_1164.all;

entity cnt_up_mod10_alarg is
  port(
    clk, z  : in  std_logic;					-- entradas clk, rst
    q       : out std_logic_vector(3 downto 0)	-- saída q3 até q0
 );
end cnt_up_mod10_alarg;

architecture cnt_up_mod10_alarg_arch of cnt_up_mod10_alarg is
	signal zn, clr_signal, prs_signal, clkn, clr_signal_alarg, qn_alarg: std_logic;
	signal qn, q_signal: std_logic_vector(3 downto 0);	-- liga qn com d
	component dff_vhdl is					-- dff referenciado como dff_vhdl
		port
		(
			d, clk, prs, clr	: in  std_logic;	-- entradas: dado, clk, preset e clear
			q, qn			: out std_logic 	-- saídas:   q e q invertido
		);
	end component;
begin
	zn <= not z;
	clkn <= not clk;
	ff_d0: dff_vhdl port map(d => qn(0), prs => '0', clr => clr_signal, clk => clk,   q => q_signal(0), qn => qn(0));
	ff_d1: dff_vhdl port map(d => qn(1), prs => '0', clr => clr_signal, clk => qn(0), q => q_signal(1), qn => qn(1));
	ff_d2: dff_vhdl port map(d => qn(2), prs => '0', clr => clr_signal, clk => qn(1), q => q_signal(2), qn => qn(2));
	ff_d3: dff_vhdl port map(d => qn(3), prs => '0', clr => clr_signal, clk => qn(2), q => q_signal(3), qn => qn(3));
	ff_alarg: dff_vhdl port map(d => '0', prs => prs_signal, clr => clkn, clk => '0', q => clr_signal_alarg, qn => qn_alarg);
	prs_signal <= (((not q_signal(0)) and q_signal(1)) and (not q_signal(2))) and q_signal(3);
	clr_signal <= (zn or (q_signal(1) and q_signal(3))) or clr_signal_alarg;
	q <= q_signal;
end cnt_up_mod10_alarg_arch;

// VHDL entity cnt_up_mod6_alarg, as the project stores it:
library ieee;
  use ieee.std_logic_1164.all;

entity cnt_up_mod6_alarg is
  port(
    clk, z  : in  std_logic;					-- entradas clk, rst
    q       : out std_logic_vector(3 downto 0)	-- saída q3 até q0
 );
end cnt_up_mod6_alarg;

architecture cnt_up_mod6_alarg_arch of cnt_up_mod6_alarg is
	signal zn, clr_signal, prs_signal, clkn, clr_signal_alarg, qn_alarg: std_logic;
	signal qn, q_signal: std_logic_vector(3 downto 0);	-- liga qn com d
	component dff_vhdl is					-- dff referenciado como dff_vhdl
		port
		(
			d, clk, prs, clr	: in  std_logic;	-- entradas: dado, clk, preset e clear
			q, qn			: out std_logic 	-- saídas:   q e q invertido
		);
	end component;
begin
	zn <= not z;
	clkn <= not clk;
	ff_d0: dff_vhdl port map(d => qn(0), prs => '0', clr => clr_signal, clk => clk,   q => q_signal(0), qn => qn(0));
	ff_d1: dff_vhdl port map(d => qn(1), prs => '0', clr => clr_signal, clk => qn(0), q => q_signal(1), qn => qn(1));
	ff_d2: dff_vhdl port map(d => qn(2), prs => '0', clr => clr_signal, clk => qn(1), q => q_signal(2), qn => qn(2));
	ff_alarg: dff_vhdl port map(d => '0', prs => prs_signal, clr => clkn, clk => '0', q => clr_signal_alarg, qn => qn_alarg);
	prs_signal <= ((not q_signal(0)) and q_signal(1)) and q_signal(2);
	clr_signal <= (zn or (q_signal(1) and q_signal(2))) or clr_signal_alarg;
	q_signal(3) <= '0';
	q <= q_signal;
end cnt_up_mod6_alarg_arch;

// VHDL entity cnt_down_mod10_alarg, as the project stores it:
library ieee;
use ieee.std_logic_1164.all;

entity cnt_down_mod10_alarg is
    port(
        clk, z : in  std_logic;
        q      : out std_logic_vector(3 downto 0)
    );
end cnt_down_mod10_alarg;

architecture cnt_down_mod10_alarg_arch of cnt_down_mod10_alarg is
    signal zn, clrn, rstd, q_rstd, prs_rstd, qn_rstd, d_rstd, clk_rstd, q_alarg, qn_alarg, clr_signal, clkn, prs_signal: std_logic;
    signal qn, q_signal: std_logic_vector(3 downto 0);
    
    component dff_vhdl is
        port (
            d, clk, prs, clr : in  std_logic;
            q, qn            : out std_logic
        );
    end component;
    
begin
	clkn <= not clk;
	zn <= not z;
    	ff_d0: dff_vhdl port map(d => qn(0), prs => clrn, clr => clr_signal, clk => clk,  q => q_signal(0), qn => qn(0));
	ff_d1: dff_vhdl port map(d => qn(1), prs => '0', clr => clrn, clk => q_signal(0), q => q_signal(1), qn => qn(1));
	ff_d2: dff_vhdl port map(d => qn(2), prs => '0', clr => clrn, clk => q_signal(1), q => q_signal(2), qn => qn(2));
	ff_d3: dff_vhdl port map(d => qn(3), prs => clrn, clr => clr_signal, clk => q_signal(2), q => q_signal(3), qn => qn(3));
	ff_rstd: dff_vhdl port map(d => d_rstd, prs => prs_rstd, clr => rstd, clk => clk_rstd, q => q_rstd, qn => qn_rstd);
	ff_alarg: dff_vhdl port map(d => '0', prs => prs_signal, clr => clkn, clk => '0', q => q_alarg, qn => qn_alarg);
	rstd <= q_rstd and (q_signal(0) and q_signal(1) and q_signal(2) and q_signal(3));
	prs_rstd <= not (q_signal(0) or q_signal(1) or q_signal(2) or q_signal(3));
   	prs_signal <= (((not q_signal(0)) and q_signal(1)) and (not q_signal(2))) and q_signal(3);
   	clr_signal <= zn or q_alarg;
	clrn <= clr_signal or rstd;
	q <= q_signal;
end cnt_down_mod10_alarg_arch;

// VHDL entity cnt_down_mod6_alarg, as the project stores it:
library ieee;
use ieee.std_logic_1164.all;

entity cnt_down_mod6_alarg is
    port(
        clk, z : in  std_logic;
        q      : out std_logic_vector(3 downto 0)
    );
end cnt_down_mod6_alarg;

architecture cnt_down_mod6_alarg_arch of cnt_down_mod6_alarg is
    signal zn, clrn, rstd, q_rstd, prs_rstd, qn_rstd, q_alarg, qn_alarg, clr_signal, clkn, prs_signal: std_logic;
    signal qn, q_signal: std_logic_vector(3 downto 0);
    
    component dff_vhdl is
        port (
            d, clk, prs, clr : in  std_logic;
            q, qn            : out std_logic
        );
    end component;
    
begin
	clkn <= not clk;
	zn <= not z;
    	ff_d0: dff_vhdl port map(d => qn(0), prs => clrn, clr => zn, clk => clk,  q => q_signal(0), qn => qn(0));
	ff_d1: dff_vhdl port map(d => qn(1), prs => '0', clr => clrn, clk => q_signal(0), q => q_signal(1), qn => qn(1));
	ff_d2: dff_vhdl port map(d => qn(2), prs => clrn, clr => zn, clk => q_signal(1), q => q_signal(2), qn => qn(2));
	ff_rstd: dff_vhdl port map(d => '0', prs => prs_rstd, clr => rstd, clk => '0', q => q_rstd, qn => qn_rstd);
	ff_alarg: dff_vhdl port map(d => '0', prs => prs_signal, clr => clkn, clk => '0', q => q_alarg, qn => qn_alarg);
	rstd <= q_rstd and (q_signal(0) and q_signal(1) and q_signal(2));
	prs_rstd <= not (q_signal(0) or q_signal(1) or q_signal(2));
   	prs_signal <= ((not q_signal(0)) and q_signal(1)) and q_signal(2);
   	clr_signal <= zn or q_alarg;
	clrn <= clr_signal or rstd;
	q_signal(3) <= '0';
	q <= q_signal;
end cnt_down_mod6_alarg_arch;

// VHDL entity cnt_up_down_mod10, as the project stores it:
library ieee;
use ieee.std_logic_1164.all;

entity cnt_up_down_mod10 is
    port(
        clk, z, ud : in  std_logic;
        q          : out std_logic_vector(3 downto 0);
        co         : out std_logic
    );
end cnt_up_down_mod10;

architecture cnt_up_down_mod10_arch of cnt_up_down_mod10 is
    signal zn, clkn, rst_down, rst_up, rst1, rst2, f, zr, r, alarg, q_alarg, qn_alarg, q_down, qn_down: std_logic;
    signal qn, q_signal: std_logic_vector(3 downto 0);
    signal mux: std_logic_vector(2 downto 0);
    
    component dff_vhdl is
        port (
            d, clk, prs, clr : in  std_logic;
            q, qn            : out std_logic
        );
    end component;
    
begin
    	ff_d0: dff_vhdl port map(d => qn(0), prs => rst_down, clr => rst1, clk => clk,  q => q_signal(0), qn => qn(0));
	ff_d1: dff_vhdl port map(d => qn(1), prs => '0', clr => rst2, clk => mux(0), q => q_signal(1), qn => qn(1));
	ff_d2: dff_vhdl port map(d => qn(2), prs => '0', clr => rst2, clk => mux(1), q => q_signal(2), qn => qn(2));
	ff_d3: dff_vhdl port map(d => qn(3), prs => rst_down, clr => rst1, clk => mux(2), q => q_signal(3), qn => qn(3));
	ff_down: dff_vhdl port map(d => '0', prs => zr, clr => rst_down, clk => '0', q => q_down, qn => qn_down);
	ff_alarg: dff_vhdl port map(d => '0', prs => alarg, clr => clkn, clk => '0', q => q_alarg, qn => qn_alarg);
	
	zn <= not z;
	clkn <= not clk;
	mux(0) <= qn(0) when (ud = '0') else
			q_signal(0) when (ud = '1');
	mux(1) <= qn(1) when (ud = '0') else
			q_signal(1) when (ud = '1');
	mux(2) <= qn(2) when (ud = '0') else
			q_signal(2) when (ud = '1');
	alarg <= (((not q_signal(0)) and q_signal(1)) and (not q_signal(2))) and q_signal(3);
	f <= ((q_signal(0) and q_signal(1)) and q_signal(2)) and q_signal(3);
	zr <= not (q_signal(0) or q_signal(1) or q_signal(2) or q_signal(3));
	rst_down <= (q_down and f) and ud;
	rst_up <= (q_signal(1) and q_signal(3)) and (not ud);
	rst1 <= zn or rst_up or q_alarg;
	rst2 <= rst1 or rst_down;
	co <= rst2;
	q <= q_signal;
end cnt_up_down_mod10_arch;

// VHDL entity cnt_up_down_mod6, as the project stores it:
library ieee;
use ieee.std_logic_1164.all;

entity cnt_up_down_mod6 is
    port(
        clk, z, ud : in  std_logic;
        q          : out std_logic_vector(3 downto 0)
    );
end cnt_up_down_mod6;

architecture cnt_up_down_mod6_arch of cnt_up_down_mod6 is
    signal zn, clkn, rst_down, rst_up, rst1, rst2, f, zr, r, alarg, q_alarg, qn_alarg, q_down, qn_down: std_logic;
    signal qn, q_signal: std_logic_vector(3 downto 0);
    signal mux: std_logic_vector(1 downto 0);
    
    component dff_vhdl is
        port (
            d, clk, prs, clr : in  std_logic;
            q, qn            : out std_logic
        );
    end component;
    
begin
    	ff_d0: dff_vhdl port map(d => qn(0), prs => rst_down, clr => rst1, clk => clk,  q => q_signal(0), qn => qn(0));
	ff_d1: dff_vhdl port map(d => qn(1), prs => '0', clr => rst2, clk => mux(0), q => q_signal(1), qn => qn(1));
	ff_d2: dff_vhdl port map(d => qn(2), prs => '0', clr => rst1, clk => mux(1), q => q_signal(2), qn => qn(2));
	ff_down: dff_vhdl port map(d => '0', prs => zr, clr => rst_down, clk => '0', q => q_down, qn => qn_down);
	ff_alarg: dff_vhdl port map(d => '0', prs => alarg, clr => clkn, clk => '0', q => q_alarg, qn => qn_alarg);
	
	zn <= not z;
	clkn <= not clk;
	mux(0) <= qn(0) when (ud = '0') else
			q_signal(0) when (ud = '1');
	mux(1) <= qn(1) when (ud = '0') else
			q_signal(1) when (ud = '1');
	alarg <= ((not q_signal(0)) and q_signal(1)) and q_signal(2);
	f <= (q_signal(0) and q_signal(1)) and q_signal(2);
	zr <= not (q_signal(0) or q_signal(1) or q_signal(2));
	rst_down <= (q_down and f) and ud;
	rst_up <= (q_signal(1) and q_signal(2)) and (not ud);
	rst1 <= zn or rst_up or q_alarg;
	rst2 <= rst1 or rst_down;
	q_signal(3) <= '0';
	q <= q_signal;
end cnt_up_down_mod6_arch;

// VHDL entity cnt_up_down_mod60, as the project stores it:
library ieee;
use ieee.std_logic_1164.all;

entity cnt_up_down_mod60 is
    port(
        clk, z, ud, sst : in  std_logic;
        qu, qd          : out std_logic_vector(3 downto 0)
    );
end cnt_up_down_mod60;

architecture cnt_up_down_mod60_arch of cnt_up_down_mod60 is
    signal co_signal, clk_signal, status, zn, q_sst, qn_sst: std_logic;
    
    component dff_vhdl is
        port (
            d, clk, prs, clr : in  std_logic;
            q, qn            : out std_logic
        );
    end component;

    component cnt_up_down_mod10_vhdl10 is
    	port (
        clk, z, ud : in  std_logic;
        q          : out std_logic_vector(3 downto 0);
        co         : out std_logic
    	);
    end component;

    component cnt_up_down_mod6_vhdl6 is
    	port (
        clk, z, ud : in  std_logic;
        q          : out std_logic_vector(3 downto 0)
    	);
    end component;
begin
	ff_unidade: cnt_up_down_mod10_vhdl10 port map(clk => clk_signal, z => z, ud => ud, co => co_signal, q => qu);
	ff_dezena: cnt_up_down_mod6_vhdl6 port map(clk => co_signal, z => z, ud => ud, q => qd);
	ff_sst: dff_vhdl port map(d => qn_sst, clk => sst, prs => '0', clr => zn, q => q_sst, qn => qn_sst);

	zn <= not z;
	clk_signal <= clk and q_sst;
end cnt_up_down_mod60_arch;

// VHDL entity cnt_ud_mod60_att, as the project stores it:
library ieee;
use ieee.std_logic_1164.all;

entity cnt_up_down_mod60 is
    port(
        clk, z, ud, sst_button, clk_50m : in  std_logic;
        disp_d, disp_u          : out std_logic_vector(6 downto 0)
    );
end cnt_up_down_mod60;

architecture cnt_up_down_mod60_arch of cnt_up_down_mod60 is
    	signal co_signal, clk_signal, status, zn, q_sst, qn_sst, clk_1s, clk_10ms, sst_deb, clk_50m_signal: std_logic;
 	signal qu, qd          : out std_logic_vector(3 downto 0);
	COMPONENT div_clk IS
		GENERIC(divisor : INTEGER := 5);
		PORT(
			clk_in  : IN STD_LOGIC; -- clock in
			clk_out : OUT STD_LOGIC -- clock divided
		);
	END COMPONENT;
	
	COMPONENT debounce IS
		GENERIC(counter_size : INTEGER := 1); -- generalizes counter capacity
		PORT(
			clk    : IN STD_LOGIC; -- clock in
			button : IN STD_LOGIC; -- input signal
			result : OUT STD_LOGIC -- debounced signal
		);
	END COMPONENT;
    
    component dff_vhdl is
        port (
            d, clk, prs, clr : in  std_logic;
            q, qn            : out std_logic
        );
    end component;

    component cnt_up_down_mod10_vhdl10 is
    	port (
        clk_button, clk_50m, z, ud : in  std_logic;
        q          : out std_logic_vector(3 downto 0);
        co         : out std_logic
    	);
    end component;

    component cnt_up_down_mod6_vhdl6 is
    	port (
        clk, z, ud : in  std_logic;
        q          : out std_logic_vector(3 downto 0)
    	);
    end component;
begin
	clk_50m_signal <= clk_50m;
	
	clk_div_10ms : div_clk GENERIC MAP(divisor => 250000)
					       PORT MAP(clk_in => clk_50m_signal, clk_out => clk_10ms);
					   
	deb : debounce 	       PORT MAP(clk => clk_10ms, button => sst_button, result => sst_deb);
	ff_unidade: cnt_up_down_mod10_vhdl10 port map(clk => clk_signal, z => z, ud => ud, co => co_signal, q => qu);
	ff_dezena: cnt_up_down_mod6_vhdl6 port map(clk => co_signal, z => z, ud => ud, q => qd);
	ff_sst: dff_vhdl port map(d => qn_sst, clk => sst_deb, prs => '0', clr => zn, q => q_sst, qn => qn_sst);
	zn <= not z;
	clk_signal <= clk and q_sst;
	WITH qd SELECT
	disp_d <= "1111110" WHEN "0000",
		   "0110000" WHEN "0001",
		   "1101101" WHEN "0010",
		   "1111001" WHEN "0011",
		   "0110011" WHEN "0100",
		   "1011011" WHEN "0101",
		   "1011111" WHEN "0110",
		   "1110000" WHEN "0111",
		   "1111111" WHEN "1000",
		   "1110011" WHEN "1001",
		   "1110111" WHEN "1010",
		   "0011111" WHEN "1011",
		   "1001110" WHEN "1100",
		   "0111101" WHEN "1101",
		   "1110000" WHEN "1110",
		   "0111100" WHEN "1111",
		   "0000000" WHEN others;
	WITH qu SELECT
	disp_u <= "1111110" WHEN "0000",
		   "0110000" WHEN "0001",
		   "1101101" WHEN "0010",
		   "1111001" WHEN "0011",
		   "0110011" WHEN "0100",
		   "1011011" WHEN "0101",
		   "1011111" WHEN "0110",
		   "1110000" WHEN "0111",
		   "1111111" WHEN "1000",
		   "1110011" WHEN "1001",
		   "1110111" WHEN "1010",
		   "0011111" WHEN "1011",
		   "1001110" WHEN "1100",
		   "0111101" WHEN "1101",
		   "1110000" WHEN "1110",
		   "0111100" WHEN "1111",
		   "0000000" WHEN others;
end cnt_up_down_mod60_arch;

// VHDL entity debounce, as the project stores it:
--------------------------------------------------------------------------------
--
--   FileName:         debounce.vhd
--   Dependencies:     none
--   Design Software:  Quartus II 32-bit Version 11.1 Build 173 SJ Full Version
--
--   HDL CODE IS PROVIDED "AS IS."  DIGI-KEY EXPRESSLY DISCLAIMS ANY
--   WARRANTY OF ANY KIND, WHETHER EXPRESS OR IMPLIED, INCLUDING BUT NOT
--   LIMITED TO, THE IMPLIED WARRANTIES OF MERCHANTABILITY, FITNESS FOR A
--   PARTICULAR PURPOSE, OR NON-INFRINGEMENT. IN NO EVENT SHALL DIGI-KEY
--   BE LIABLE FOR ANY INCIDENTAL, SPECIAL, INDIRECT OR CONSEQUENTIAL
--   DAMAGES, LOST PROFITS OR LOST DATA, HARM TO YOUR EQUIPMENT, COST OF
--   PROCUREMENT OF SUBSTITUTE GOODS, TECHNOLOGY OR SERVICES, ANY CLAIMS
--   BY THIRD PARTIES (INCLUDING BUT NOT LIMITED TO ANY DEFENSE THEREOF),
--   ANY CLAIMS FOR INDEMNITY OR CONTRIBUTION, OR OTHER SIMILAR COSTS.
--
--   Version History
--   Version 1.0 3/26/2012 Scott Larson
--     Initial Public Release
--
--------------------------------------------------------------------------------

LIBRARY ieee;
USE ieee.std_logic_1164.all;
USE ieee.std_logic_unsigned.all;

ENTITY debounce IS
  GENERIC(counter_size  :  INTEGER := 1); -- generaliza capacidade do contador
  PORT(
    clk     : IN  STD_LOGIC;  --entrada relógio
    button  : IN  STD_LOGIC;  --input signal to be debounced
    result  : OUT STD_LOGIC);
END debounce;

ARCHITECTURE logic OF debounce IS
  SIGNAL flipflops   : STD_LOGIC_VECTOR(1 DOWNTO 0); -- flip-flops FF0 e FF1
  SIGNAL counter_set : STD_LOGIC;                    -- condição xor para reset síncrono
  SIGNAL counter_out : STD_LOGIC_VECTOR(counter_size DOWNTO 0) := (OTHERS => '0');
BEGIN

  counter_set <= flipflops(0) xor flipflops(1);   -- reseta cnt se amostras diferem
  
  PROCESS(clk)
  BEGIN
    IF(clk'EVENT and clk = '1') THEN
      flipflops(0) <= button;
      flipflops(1) <= flipflops(0);
      If(counter_set = '1') THEN                  -- reseta contador se amostras diferem
        counter_out <= (OTHERS => '0');
	  ELSIF counter_out /= "11" THEN
        counter_out <= counter_out + 1;
      ELSE                                        -- contagem estabilizada foi atingida
        result <= flipflops(1);
      END IF;    
    END IF;
  END PROCESS;
END logic;

// VHDL entity div_clk, as the project stores it:
--------------------------------------------------------------------------------
-- UTFPR - Universidade Tecnol�gica Federal do Paraná - Curitiba - PR
-- Projeto : Divisor de frequência
-- Arquivo : basic_divider.vhd
-- Autor   : prof. Gortan
-- Data    : Abril 2020
--
----------------------------------------------------------------------------
-- Descrição :
-- divisor de frequência genérico
----------------------------------------------------------------------------

library ieee;
  use ieee.std_logic_1164.all;

entity div_clk is
  generic(divisor: integer := 5);
  port(
    clk_in		: in  std_logic;	-- clock in.
    clk_out		: out std_logic		-- clock in dividido 2 x divisor
    );
end div_clk;
----------------------------------------------------------------------------
architecture divisor of div_clk is
signal temp: std_logic :='0';
begin

	P_div:process (clk_in)                                              
	variable count:integer range 0 to divisor;
	begin                                                                
		if clk_in'event and clk_in = '1' then
			count := count + 1;
			if (count = divisor) then
				temp <= not temp;
				count := 0;
			end if;
		 end if; 
	end process P_div;
	clk_out <= temp;                                    

end divisor;
