// Logisim project pratica6.circ as structural Verilog
module circuito1 (
  input  in_1,
  output [6:0] out_2,
  output [6:0] out_3
);

  wire button_1_out, button_2_out, clock_1_out, not_1_out, not_2_out, not_3_out;

  Clock clock_1 (.out(clock_1_out));
  Button button_1 (.out(button_1_out));
  Button button_2 (.out(button_2_out));
  not not_1 (not_1_out, button_1_out);
  not not_2 (not_2_out, button_2_out);
  not not_3 (not_3_out, in_1);
  cronometro cronometro_1 (
    .clk(clock_1_out), .start_stop(not_1_out), .ud(not_2_out), .z(not_3_out), .dezena(out_2), .unidade(out_3));
  _7_Segment_Display u_7_segment_display_1 (
    .g(out_2[0]), .f(out_2[1]), .a(out_2[6]), .b(out_2[5]), .e(out_2[2]), .d(out_2[3]), .c(out_2[4]));  // open: dp
  _7_Segment_Display u_7_segment_display_2 (
    .g(out_3[0]), .f(out_3[1]), .a(out_3[6]), .b(out_3[5]), .e(out_3[2]), .d(out_3[3]), .c(out_3[4]));  // open: dp
endmodule

module circuito2 (
  output [6:0] out_1,
  output [6:0] out_2
);

  wire button_1_out, clock_1_out, not_1_out;

  Clock clock_1 (.out(clock_1_out));
  not not_1 (not_1_out, button_1_out);
  Button button_1 (.out(button_1_out));
  sequencia sequencia_1 (.clk(clock_1_out), .start(not_1_out), .msd(out_1), .lsd(out_2));
  _7_Segment_Display u_7_segment_display_1 (
    .g(out_1[0]), .f(out_1[1]), .a(out_1[6]), .b(out_1[5]), .e(out_1[2]), .d(out_1[3]), .c(out_1[4]));  // open: dp
  _7_Segment_Display u_7_segment_display_2 (
    .g(out_2[0]), .f(out_2[1]), .a(out_2[6]), .b(out_2[5]), .e(out_2[2]), .d(out_2[3]), .c(out_2[4]));  // open: dp
endmodule

// VHDL entity cronometro, as the project stores it:
library IEEE;
use IEEE.STD_LOGIC_1164.ALL;
use IEEE.NUMERIC_STD.ALL;

entity cronometro is
    Port( 
        clk : in STD_LOGIC;
        start_stop : in STD_LOGIC;
        ud : in STD_LOGIC;
        z : in STD_LOGIC;
        dezena : out STD_LOGIC_VECTOR(6 downto 0);
        unidade : out STD_LOGIC_VECTOR(6 downto 0)
    );
end cronometro;

architecture cronometro_arch of cronometro is
    signal contagem : INTEGER range 0 to 59 := 0;
    signal start_stop_ff : STD_LOGIC := '1'; -- 0=off, 1=on
    signal ud_ff : STD_LOGIC := '0'; -- 0=up, 1=down

    function DISPLAY(num : INTEGER) return STD_LOGIC_VECTOR is
    begin
        case num is
            when 0 => return "1111110";
            when 1 => return "0110000";
            when 2 => return "1101101";
            when 3 => return "1111001";
            when 4 => return "0110011";
            when 5 => return "1011011";
            when 6 => return "1011111";
            when 7 => return "1110000";
            when 8 => return "1111111";
            when 9 => return "1110011";
            when others => return "0000000";
        end case;
    end DISPLAY;

begin
    process (clk, z, ud, start_stop)
    begin
        if (z = '0' and rising_edge(ud)) then
            ud_ff <= ud_ff XOR '1';
        end if;
        if (rising_edge(start_stop)) then
            start_stop_ff <= start_stop_ff XOR '1';
        end if;
        if (rising_edge(z)) then
            if(ud_ff = '0') then
                contagem <= 0;
            else
                contagem <= 59;
            end if;
        end if;
        if (rising_edge(clk) and start_stop_ff = '1') then
            if (ud_ff = '0') then
                if (contagem = 59) then
                    contagem <= 0;
                else
                    contagem <= contagem + 1;
                end if;
            else
                if (contagem = 0) then
                    contagem <= 59;
                else
                    contagem <= contagem - 1;
                end if;
            end if;
        end if;
    end process;
    dezena <= DISPLAY(contagem/10);
    unidade <= DISPLAY(contagem mod 10);
end cronometro_arch;

// VHDL entity sequencia, as the project stores it:
library IEEE;
use IEEE.STD_LOGIC_1164.ALL;
use IEEE.NUMERIC_STD.ALL;

entity sequencia is
    Port( 
        clk : in STD_LOGIC;
        start : in STD_LOGIC;
        msd : out STD_LOGIC_VECTOR(6 downto 0);
        lsd : out STD_LOGIC_VECTOR(6 downto 0)
    );
end sequencia;

architecture sequencia_arch of sequencia is
    signal contagem_lsd : INTEGER range 0 to 8 := 0;
    signal contagem_msd : STD_LOGIC := '0';
    signal ud_lsd : STD_LOGIC := '0'; -- 0=up, 1=down
    signal start_signal : STD_LOGIC := '0'; -- 0=off, 1=on

    function DISPLAY_LSD(num : integer) return STD_LOGIC_VECTOR is
    begin
        case num is
        	when 0 => return "0000001"; -- simbolo "-"
            when 1 => return "1101101"; -- numero 2
            when 2 => return "1011011"; -- numero 5
            when 3 => return "0110000"; -- numero 1
            when 4 => return "1011111"; -- numero 6
            when 5 => return "1110011"; -- numero 9
            when 6 => return "1110000"; -- numero 7
            when 7 => return "1110000"; -- numero 7
            when 8 => return "0000001"; -- simbolo "-"
            when others => return "0000001";
        end case;
    end DISPLAY_LSD;

    function DISPLAY_MSD(num2 : STD_LOGIC) return STD_LOGIC_VECTOR is
    begin
        case num2 is
            when '0' => return "0000000";
            when '1' => return "0111100"; -- letra J
            when others => return "0000000";
        end case;
    end DISPLAY_MSD;

begin
	process (clk, start)
	begin
	    if rising_edge(start) then
	        start_signal <= start_signal XOR '1';
	    end if;
	    if rising_edge(clk) then
	        if start_signal = '1' then
	        	  contagem_msd <= contagem_msd XOR '1';
	            if (ud_lsd = '0') then
	                if (contagem_lsd < 8) then
	                    contagem_lsd <= contagem_lsd + 1;
	                else
	                    contagem_lsd <= 7;
	                    ud_lsd <= '1';
	                end if;
	            elsif (ud_lsd = '1') then
	                if (contagem_lsd > 0) then
	                    contagem_lsd <= contagem_lsd - 1;
	                else
	                    start_signal <= '0';
	                    ud_lsd <= '0';
	                    contagem_msd <= '0';
	                end if;
	            end if;
	        end if;
	    end if;
	end process;
     msd <= DISPLAY_MSD(contagem_msd);
     lsd <= DISPLAY_LSD(contagem_lsd);
end sequencia_arch;
