// Logisim project detector.circ as structural Verilog
module main (
  input  [5:0] SEQ
);

  wire CLK_out, RST_out;
  wire [3:0] undriven, undriven_2;

  Button RST (.out(RST_out));
  Clock CLK (.out(CLK_out));
  Hex_Digit_Display hex_digit_display_1 (.value(undriven));  // open: dp
  Hex_Digit_Display hex_digit_display_2 (.value(undriven_2));  // open: dp
endmodule

module v1 (
  input  SEQ
);

  wire and_1_out, CLK_out, not_1_out, RST_out;
  wire [2:0] bloco_comb_mux8_1_prx_est, bloco_sequencial_1_est_prs;
  wire [3:0] multiplexer_1_out, seq_compr_fixo_1_1_est_out, seq_compr_fixo_1_1_res_out;

  Clock CLK (.out(CLK_out));
  Button RST (.out(RST_out));
  not not_1 (not_1_out, RST_out);
  bloco_comb_mux8 bloco_comb_mux8_1 (
    .SEQ_IN(SEQ), .EST_PRS(bloco_sequencial_1_est_prs), .PRX_EST(bloco_comb_mux8_1_prx_est));
  bloco_sequencial bloco_sequencial_1 (
    .PRX_EST(bloco_comb_mux8_1_prx_est), .CLK(CLK_out), .RST(not_1_out), .EST_PRS(bloco_sequencial_1_est_prs));
  Hex_Digit_Display hex_digit_display_1 (.value(seq_compr_fixo_1_1_res_out));  // open: dp
  seq_compr_fixo_1 seq_compr_fixo_1_1 (
    .rst(RST_out), .seq_in(SEQ), .clock(CLK_out), .res_out(seq_compr_fixo_1_1_res_out),
    .est_out(seq_compr_fixo_1_1_est_out));
  Hex_Digit_Display hex_digit_display_2 (.value(seq_compr_fixo_1_1_est_out));  // open: dp
  Hex_Digit_Display hex_digit_display_3 (.value(multiplexer_1_out));  // open: dp
  Multiplexer #(.width(4)) multiplexer_1 (.in0(4'b0000), .in1(4'b0001), .out(multiplexer_1_out), .sel(and_1_out));
  and and_1 (and_1_out, bloco_sequencial_1_est_prs[0], ~bloco_sequencial_1_est_prs[1], bloco_sequencial_1_est_prs[2]);  // AND_Gate
  Hex_Digit_Display hex_digit_display_4 (.value({1'b0, bloco_sequencial_1_est_prs}));  // open: dp
endmodule

module v2 (
  input  SEQ
);

  wire and_1_out, CLK_out, not_1_out, RST_out;
  wire [2:0] bloco_comb_mux8_1_prx_est, bloco_sequencial_1_est_prs;
  wire [3:0] detector_seq_1_est_out, detector_seq_1_res_out, multiplexer_1_out;

  Clock CLK (.out(CLK_out));
  Button RST (.out(RST_out));
  not not_1 (not_1_out, RST_out);
  bloco_comb_mux8 bloco_comb_mux8_1 (
    .SEQ_IN(SEQ), .EST_PRS(bloco_sequencial_1_est_prs), .PRX_EST(bloco_comb_mux8_1_prx_est));
  bloco_sequencial bloco_sequencial_1 (
    .PRX_EST(bloco_comb_mux8_1_prx_est), .CLK(CLK_out), .RST(not_1_out), .EST_PRS(bloco_sequencial_1_est_prs));
  detector_seq detector_seq_1 (
    .rst(RST_out), .seq_in(SEQ), .clock(CLK_out), .res_out(detector_seq_1_res_out),
    .est_out(detector_seq_1_est_out));
  seq_compr_fixo_2 vhdl ();  // open: rst, seq_in, clock, res_out, est_out
  Hex_Digit_Display hex_digit_display_1 (.value(detector_seq_1_res_out));  // open: dp
  Hex_Digit_Display hex_digit_display_2 (.value(detector_seq_1_est_out));  // open: dp
  Hex_Digit_Display hex_digit_display_3 (.value(multiplexer_1_out));  // open: dp
  Multiplexer #(.width(4)) multiplexer_1 (.in0(4'b0000), .in1(4'b0001), .out(multiplexer_1_out), .sel(and_1_out));
  and and_1 (and_1_out, bloco_sequencial_1_est_prs[0], ~bloco_sequencial_1_est_prs[1], bloco_sequencial_1_est_prs[2]);  // AND_Gate
  Hex_Digit_Display hex_digit_display_4 (.value({1'b0, bloco_sequencial_1_est_prs}));  // open: dp
endmodule

module v3 (
  input  SEQ
);

  wire and_1_out, CLK_out, not_1_out, RST_out;
  wire [2:0] bloco_comb_mux8_1_prx_est, bloco_sequencial_1_est_prs;
  wire [3:0] multiplexer_1_out, seq_compr_vari_1_est_out, seq_compr_vari_1_res_out;

  Clock CLK (.out(CLK_out));
  Button RST (.out(RST_out));
  not not_1 (not_1_out, RST_out);
  bloco_comb_mux8 bloco_comb_mux8_1 (
    .SEQ_IN(SEQ), .EST_PRS(bloco_sequencial_1_est_prs), .PRX_EST(bloco_comb_mux8_1_prx_est));
  bloco_sequencial bloco_sequencial_1 (
    .PRX_EST(bloco_comb_mux8_1_prx_est), .CLK(CLK_out), .RST(not_1_out), .EST_PRS(bloco_sequencial_1_est_prs));
  seq_compr_vari seq_compr_vari_1 (
    .rst(RST_out), .seq_in(SEQ), .clock(CLK_out), .res_out(seq_compr_vari_1_res_out),
    .est_out(seq_compr_vari_1_est_out));
  Hex_Digit_Display hex_digit_display_1 (.value(seq_compr_vari_1_res_out));  // open: dp
  Hex_Digit_Display hex_digit_display_2 (.value(seq_compr_vari_1_est_out));  // open: dp
  Hex_Digit_Display hex_digit_display_3 (.value(multiplexer_1_out));  // open: dp
  Multiplexer #(.width(4)) multiplexer_1 (.in0(4'b0000), .in1(4'b0001), .out(multiplexer_1_out), .sel(and_1_out));
  and and_1 (and_1_out, bloco_sequencial_1_est_prs[0], ~bloco_sequencial_1_est_prs[1], bloco_sequencial_1_est_prs[2]);  // AND_Gate
  Hex_Digit_Display hex_digit_display_4 (.value({1'b0, bloco_sequencial_1_est_prs}));  // open: dp
endmodule

module bloco_sequencial (
  input  [2:0] PRX_EST,
  input  CLK,
  input  RST,
  output [2:0] EST_PRS
);

  Register #(.width(3)) register_1 (.D(PRX_EST), .clk(CLK), .Q(EST_PRS), .clr(RST));  // open: en
endmodule

module bloco_comb_mux8 (
  input  SEQ_IN,
  input  [2:0] EST_PRS,
  output [2:0] PRX_EST
);

  wire [1:1] not_1_out;

  not not_1 (not_1_out[1], SEQ_IN);
  Multiplexer #(.select(3), .width(3)) multiplexer_1 (
    .in0({2'b00, SEQ_IN}), .in1({1'b0, SEQ_IN, 1'b0}), .in2({1'b0, {2{not_1_out[1]}}}),
    .in3({not_1_out[1], 2'b00}), .in4({SEQ_IN, 1'b0, SEQ_IN}), .in5({{2{not_1_out[1]}}, 1'b0}), .in6(3'b110),
    .in7(3'b000), .out(PRX_EST), .sel(EST_PRS));
endmodule

module bloco_comb_mux16 (
  input  SEQ_IN,
  input  [2:0] EST_PRS,
  output [2:0] PRX_EST
);

  Multiplexer #(.select(4), .width(3)) multiplexer_1 (
    .in0(3'b000), .in1(3'b001), .in2(3'b000), .in3(3'b010), .in4(3'b011), .in5(3'b000), .in6(3'b100),
    .in7(3'b000), .in8(3'b000), .in9(3'b101), .in10(3'b110), .in11(3'b000), .in12(3'b110), .in13(3'b110),
    .in14(3'b000), .in15(3'b000), .out(PRX_EST), .sel({EST_PRS, SEQ_IN}));
endmodule

module bloco_comb_prom (
  input  SEQ_IN,
  input  [2:0] EST_PRS,
  output [2:0] PRX_EST
);

  ROM #(.addrWidth(4), .dataWidth(3)) rom_1 (.addr({EST_PRS, SEQ_IN}), .data(PRX_EST));

  // Notes on the sheet:
  //   contents of rom_1 (hex, n*v repeats v):
  //   0 1 0 2 3 0 4 0 0 5 6 0 6 6
endmodule

module teste (
  input  [2:0] EST_PRS,
  input  SEQ_IN
);

  wire [2:0] bloco_comb_mux8_1_prx_est, bloco_comb_mux16_1_prx_est, bloco_comb_prom_1_prx_est;

  bloco_comb_mux16 bloco_comb_mux16_1 (.SEQ_IN(SEQ_IN), .EST_PRS(EST_PRS), .PRX_EST(bloco_comb_mux16_1_prx_est));
  bloco_comb_prom bloco_comb_prom_1 (.SEQ_IN(SEQ_IN), .EST_PRS(EST_PRS), .PRX_EST(bloco_comb_prom_1_prx_est));
  bloco_comb_mux8 bloco_comb_mux8_1 (.SEQ_IN(SEQ_IN), .EST_PRS(EST_PRS), .PRX_EST(bloco_comb_mux8_1_prx_est));
  Hex_Digit_Display hex_digit_display_1 (.value({1'b0, bloco_comb_mux16_1_prx_est}));  // open: dp
  Hex_Digit_Display hex_digit_display_2 (.value({1'b0, bloco_comb_prom_1_prx_est}));  // open: dp
  Hex_Digit_Display hex_digit_display_3 (.value({1'b0, bloco_comb_mux8_1_prx_est}));  // open: dp
endmodule

// VHDL entity seq_compr_fixo_2, as the project stores it:
LIBRARY ieee;
USE ieee.std_logic_1164.all;
use ieee.numeric_std.all;

entity seq_compr_fixo_2 is
    generic(iseq: integer := 50);
    port(
        rst, seq_in, clock : in std_logic; -- entradas clk e seq
        res_out, est_out   : out std_logic_vector(3 downto 0) -- display detectado
    );
end seq_compr_fixo_2;

architecture detector of seq_compr_fixo_2 is

type estado is (A, B, C, D, E, F); -- enumeração estados
constant seq: std_logic_vector(5 downto 0):=std_logic_vector(to_unsigned(iseq, 6));
signal estado_prs, prx_estado: estado; -- especificamos os próximos estados

-- especificamos a codificação do estado em binário (sequencial):
attribute enum_encoding: string;
attribute enum_encoding of estado: type is "sequential";


begin
	-- Bloco de lógica sequencial ---------------------------------
	seq_proc: process(clock,rst)
	begin
	    if rst = '1' then estado_prs <= A;
	    elsif clock = '1' and clock'event then
	        estado_prs <= prx_estado;
	    end if;
	end process seq_proc;
	
	-- Bloco de lógica combinacional:
	comb_proc: process (estado_prs, seq_in)
	variable idx_est, idx_seq: integer;
	begin
	    idx_est := estado'pos(estado_prs); -- obtém o índice do estado
	    idx_seq := seq'left - idx_est; -- o da seq é complementar
	    if estado_prs /= estado'right then -- se não chegou ao último estado
	    	if seq_in = seq(idx_est) then -- e se a sequência conferir
	        prx_estado <= estado'val(idx_est + 1); -- avança para próximo estado
	      else -- se não conferiu
	        prx_estado <= estado'left; -- volta ao estado inicial
	      end if;
	    else 
	      prx_estado <= estado'right; -- trava no último estado
	    end if;
	   
	    est_out <= std_logic_vector(to_unsigned(idx_est, est_out'length));
	
	-- Codificação da saída 
	case estado_prs IS 
	  when estado'right => res_out <= X"1";
	  when OTHERS => res_out <= X"0";
	end case;
	end process comb_proc;

end detector;

// VHDL entity detector_seq, as the project stores it:
LIBRARY ieee;
USE ieee.std_logic_1164.all;
use ieee.numeric_std.all;

entity detector_seq is
    port(
        rst, seq_in, clock : in std_logic;
        res_out, est_out : out std_logic_vector(3 downto 0) -- display detectado
    );
end entity detector_seq;

architecture detector of detector_seq is
    component seq_compr_fixo_2_vhdl is
        generic(iseq: integer := 50); -- valor a sobrescrever no generic_map
        port(
            rst, seq_in, clock : in std_logic;
            res_out, est_out : out std_logic_vector(3 downto 0) -- display detectado
        );
    end component;

begin
    det: seq_compr_fixo_2_vhdl generic map(iseq => 50) -- usamos o mesmo para teste
        port map(
            rst => rst,
            seq_in => seq_in,
            clock => clock,
            res_out => res_out,
            est_out => est_out
        );
end architecture detector;

// VHDL entity seq_compr_vari, as the project stores it:
LIBRARY ieee;
USE ieee.std_logic_1164.all;
use ieee.numeric_std.all;

entity seq_compr_vari is
-- o genérico abaixo permite ajustar o tamanho em bits da
-- sequência quanto ao seu valor:
generic(bits: natural := 6; seq_to_det: integer := 50);
port(
    rst, seq_in, clock : in std_logic; -- entradas rst, clk e seq
    res_out, est_out   : out std_logic_vector(3 downto 0) -- display detectado
);
end seq_compr_vari;

architecture detector of seq_compr_vari is

constant seq: std_logic_vector(bits-1 downto 0) :=
             std_logic_vector(to_unsigned(seq_to_det,bits));

signal stat_prs, prx_stat: integer range 0 to bits;

begin
	-- Bloco de lógica sequencial:
	seq_proc: process(clock, rst)
	begin
	  if rst = '1' then -- reset vai a zero
	    stat_prs <= 0;
	  elsif clock = '1' and clock'event then
	    stat_prs <= prx_stat; -- assume o próximo estado
	  end if;
	end process seq_proc;
	--------- Bloco de lógica combinacional ------------
	comb_proc: process(stat_prs, seq_in)
	variable idx_seq: integer;
	begin
	    idx_seq := bits - 1 - stat_prs; -- obtem o indice a verificar
	    if stat_prs /= bits then -- se não chegou ao último estado
	        if seq_in = seq(idx_seq) then -- e se a sequência conferir
	            prx_stat <= stat_prs + 1; -- avança para próximo estado
	        else
	            prx_stat <= 0; -- volta ao estado inicial
	        end if;
	    else
	        prx_stat <= bits; -- trava no último estado
	    end if;
	    est_out <= std_logic_vector (to_unsigned(stat_prs, est_out'length));
	    if stat_prs = bits then
	        res_out <= X"1";
	    else
	        res_out <= X"0";
	    end if;
	end process comb_proc;
end detector;

// VHDL entity seq_compr_fixo_1, as the project stores it:
LIBRARY ieee;
USE ieee.std_logic_1164.all;
use ieee.numeric_std.all;

entity seq_compr_fixo_1 is
	generic(iseq: integer := 50);
    port(
        rst, seq_in, clock : in std_logic; -- entradas clk e seq
        res_out, est_out   : out std_logic_vector(3 downto 0) -- display detectado
    );
end seq_compr_fixo_1;

architecture detector of seq_compr_fixo_1 is

type estado is (A, B, C, D, E, F, G); -- enumeração estados
	constant seq: std_logic_vector(5 downto 0):=std_logic_vector(to_unsigned(iseq, 6));
	signal estado_prs, prx_estado: estado; -- especificamos os próximos estados
	
	-- especificamos a codificação do estado em binário (sequencial):
	attribute enum_encoding: string;
	attribute enum_encoding of estado: type is "sequential";


begin
	-- Bloco de lógica sequencial ---------------------------------
	seq_proc: process(clock,rst)
	begin
	    if rst = '1' then estado_prs <= A;
	    elsif clock = '1' and clock'event then
	        estado_prs <= prx_estado;
	    end if;
	end process seq_proc;
	
	-- Bloco de lógica combinacional:
	comb_proc: process (estado_prs, seq_in)
	variable idx: integer;
	begin
	    	case estado_prs is
		    	when A =>
		    		if seq_in = seq(5) then prx_estado <= B;
		    		else prx_estado <= A;
		    		end if;
		    	WHEN B =>
		    		if seq_in = seq(4) then prx_estado <= C;
		    		else prx_estado <= A;
		    		end if;
		    	WHEN C =>
		    		if seq_in = seq(3) then prx_estado <= D;
		    		else prx_estado <= A;
		    		end if;
		    	WHEN D =>
		    		if seq_in = seq(2) then prx_estado <= E;
		    		else prx_estado <= A;
		    		end if;
		    	WHEN E =>
		    		if seq_in = seq(1) then prx_estado <= F;
		    		else prx_estado <= A;
		    		end if;
		    	WHEN F =>
		    		if seq_in = seq(0) then prx_estado <= G;
		    		else prx_estado <= A;
		    		end if;
		    	WHEN G => prx_estado <= G;
		end case;
		---- Codificação do índice do estado ----------
		idx := estado'POS(estado_prs);
		est_out <= std_logic_vector(to_unsigned(idx, est_out'length));
	
		--- Codificação da saída ----
		case estado_prs is
			when G => res_out <= X"1";
			when others => res_out <= X"0";
		end case;
	end process comb_proc;
end detector;
